// Logisim project CPU_Proj_2.circ as structural Verilog: 4 circuits, main circuit regfile
module CPUmain (
);

  regfile regfile_1 ();  // open: rs, write_e, rd, rt, rd_data, rs_data, rt_data
  Control control_1 ();  // open: Inst, rs, rt, rd, imm, reg_write_e, imm_sel, ALU_code
  ALU alu_1 ();  // open: OP1, OP2, ALU_CODE, Res
endmodule

module regfile (
  input  [31:0] rd_data,
  input  write_e,
  input  [4:0] rs,
  input  [4:0] rd,
  input  [4:0] rt,
  output [31:0] rs_data,
  output [31:0] rt_data
);

  wire clock_1_out, demultiplexer_1_out1, demultiplexer_1_out2, demultiplexer_1_out3, demultiplexer_1_out4,
       demultiplexer_1_out5, demultiplexer_1_out6, demultiplexer_1_out7, demultiplexer_1_out8,
       demultiplexer_1_out9, demultiplexer_1_out10, demultiplexer_1_out11, demultiplexer_1_out12,
       demultiplexer_1_out13, demultiplexer_1_out14, demultiplexer_1_out15, demultiplexer_1_out16,
       demultiplexer_1_out17, demultiplexer_1_out18, demultiplexer_1_out19, demultiplexer_1_out20,
       demultiplexer_1_out21, demultiplexer_1_out22, demultiplexer_1_out23, demultiplexer_1_out24,
       demultiplexer_1_out25, demultiplexer_1_out26, demultiplexer_1_out27, demultiplexer_1_out28,
       demultiplexer_1_out29, demultiplexer_1_out30, demultiplexer_1_out31;
  wire [31:0] register_1_q, register_2_q, register_3_q, register_4_q, register_5_q, register_6_q,
       register_7_q, register_8_q, register_9_q, register_10_q, register_11_q, register_12_q, register_13_q,
       register_14_q, register_15_q, register_16_q, register_17_q, register_18_q, register_19_q,
       register_20_q, register_21_q, register_22_q, register_23_q, register_25_q, register_26_q,
       register_27_q, register_28_q, register_29_q, register_30_q, register_31_q, Zero_Reg_q;

  Demultiplexer #(.select(5)) demultiplexer_1 (
    .out1(demultiplexer_1_out1), .out2(demultiplexer_1_out2), .out3(demultiplexer_1_out3),
    .out4(demultiplexer_1_out4), .out5(demultiplexer_1_out5), .out6(demultiplexer_1_out6),
    .out7(demultiplexer_1_out7), .out8(demultiplexer_1_out8), .out9(demultiplexer_1_out9),
    .out10(demultiplexer_1_out10), .out11(demultiplexer_1_out11), .out12(demultiplexer_1_out12),
    .out13(demultiplexer_1_out13), .out14(demultiplexer_1_out14), .out15(demultiplexer_1_out15),
    .out16(demultiplexer_1_out16), .out17(demultiplexer_1_out17), .out18(demultiplexer_1_out18),
    .out19(demultiplexer_1_out19), .out20(demultiplexer_1_out20), .out21(demultiplexer_1_out21),
    .out22(demultiplexer_1_out22), .out23(demultiplexer_1_out23), .out24(demultiplexer_1_out24),
    .out25(demultiplexer_1_out25), .out26(demultiplexer_1_out26), .out27(demultiplexer_1_out27),
    .out28(demultiplexer_1_out28), .out29(demultiplexer_1_out29), .out30(demultiplexer_1_out30),
    .out31(demultiplexer_1_out31), .in(write_e), .sel(rd));  // open: out0
  Clock clock_1 (.out(clock_1_out));
  Register #(.width(32)) Zero_Reg (.D({32{1'b0}}), .en(1'b1), .clk(clock_1_out), .Q(Zero_Reg_q));  // open: clr
  Register #(.width(32)) register_1 (
    .D(rd_data), .en(demultiplexer_1_out1), .clk(clock_1_out), .Q(register_1_q));  // open: clr
  Register #(.width(32)) register_2 (
    .D(rd_data), .en(demultiplexer_1_out2), .clk(clock_1_out), .Q(register_2_q));  // open: clr
  Register #(.width(32)) register_3 (
    .D(rd_data), .en(demultiplexer_1_out3), .clk(clock_1_out), .Q(register_3_q));  // open: clr
  Register #(.width(32)) register_4 (
    .D(rd_data), .en(demultiplexer_1_out4), .clk(clock_1_out), .Q(register_4_q));  // open: clr
  Register #(.width(32)) register_5 (
    .D(rd_data), .en(demultiplexer_1_out5), .clk(clock_1_out), .Q(register_5_q));  // open: clr
  Register #(.width(32)) register_6 (
    .D(rd_data), .en(demultiplexer_1_out6), .clk(clock_1_out), .Q(register_6_q));  // open: clr
  Register #(.width(32)) register_7 (
    .D(rd_data), .en(demultiplexer_1_out7), .clk(clock_1_out), .Q(register_7_q));  // open: clr
  Register #(.width(32)) register_8 (
    .D(rd_data), .en(demultiplexer_1_out8), .clk(clock_1_out), .Q(register_8_q));  // open: clr
  Register #(.width(32)) register_9 (
    .D(rd_data), .en(demultiplexer_1_out9), .clk(clock_1_out), .Q(register_9_q));  // open: clr
  Register #(.width(32)) register_10 (
    .D(rd_data), .en(demultiplexer_1_out10), .clk(clock_1_out), .Q(register_10_q));  // open: clr
  Register #(.width(32)) register_11 (
    .D(rd_data), .en(demultiplexer_1_out11), .clk(clock_1_out), .Q(register_11_q));  // open: clr
  Register #(.width(32)) register_12 (
    .D(rd_data), .en(demultiplexer_1_out12), .clk(clock_1_out), .Q(register_12_q));  // open: clr
  Register #(.width(32)) register_13 (
    .D(rd_data), .en(demultiplexer_1_out13), .clk(clock_1_out), .Q(register_13_q));  // open: clr
  Register #(.width(32)) register_14 (
    .D(rd_data), .en(demultiplexer_1_out14), .clk(clock_1_out), .Q(register_14_q));  // open: clr
  Register #(.width(32)) register_15 (
    .D(rd_data), .en(demultiplexer_1_out15), .clk(clock_1_out), .Q(register_15_q));  // open: clr
  Register #(.width(32)) register_16 (
    .D(rd_data), .en(demultiplexer_1_out16), .clk(clock_1_out), .Q(register_16_q));  // open: clr
  Register #(.width(32)) register_17 (
    .D(rd_data), .en(demultiplexer_1_out17), .clk(clock_1_out), .Q(register_17_q));  // open: clr
  Register #(.width(32)) register_18 (
    .D(rd_data), .en(demultiplexer_1_out18), .clk(clock_1_out), .Q(register_18_q));  // open: clr
  Register #(.width(32)) register_19 (
    .D(rd_data), .en(demultiplexer_1_out19), .clk(clock_1_out), .Q(register_19_q));  // open: clr
  Register #(.width(32)) register_20 (
    .D(rd_data), .en(demultiplexer_1_out20), .clk(clock_1_out), .Q(register_20_q));  // open: clr
  Register #(.width(32)) register_21 (
    .D(rd_data), .en(demultiplexer_1_out21), .clk(clock_1_out), .Q(register_21_q));  // open: clr
  Register #(.width(32)) register_22 (
    .D(rd_data), .en(demultiplexer_1_out22), .clk(clock_1_out), .Q(register_22_q));  // open: clr
  Register #(.width(32)) register_23 (
    .D(rd_data), .en(demultiplexer_1_out23), .clk(clock_1_out), .Q(register_23_q));  // open: clr
  Register #(.width(32)) register_24 (
    .D(rd_data), .en(demultiplexer_1_out24), .clk(clock_1_out), .Q(register_23_q));  // open: clr
  Register #(.width(32)) register_25 (
    .D(rd_data), .en(demultiplexer_1_out25), .clk(clock_1_out), .Q(register_25_q));  // open: clr
  Register #(.width(32)) register_26 (
    .D(rd_data), .en(demultiplexer_1_out26), .clk(clock_1_out), .Q(register_26_q));  // open: clr
  Register #(.width(32)) register_27 (
    .D(rd_data), .en(demultiplexer_1_out27), .clk(clock_1_out), .Q(register_27_q));  // open: clr
  Register #(.width(32)) register_28 (
    .D(rd_data), .en(demultiplexer_1_out28), .clk(clock_1_out), .Q(register_28_q));  // open: clr
  Register #(.width(32)) register_29 (
    .D(rd_data), .en(demultiplexer_1_out29), .clk(clock_1_out), .Q(register_29_q));  // open: clr
  Register #(.width(32)) register_30 (
    .D(rd_data), .en(demultiplexer_1_out30), .clk(clock_1_out), .Q(register_30_q));  // open: clr
  Register #(.width(32)) register_31 (
    .D(rd_data), .en(demultiplexer_1_out31), .clk(clock_1_out), .Q(register_31_q));  // open: clr
  Multiplexer #(.select(5), .width(32)) multiplexer_1 (
    .in0(Zero_Reg_q), .in1(register_1_q), .in2(register_2_q), .in3(register_3_q), .in4(register_4_q),
    .in5(register_5_q), .in6(register_6_q), .in7(register_7_q), .in8(register_8_q), .in9(register_9_q),
    .in10(register_10_q), .in11(register_11_q), .in12(register_12_q), .in13(register_13_q),
    .in14(register_14_q), .in15(register_15_q), .in16(register_16_q), .in17(register_17_q),
    .in18(register_18_q), .in19(register_19_q), .in20(register_20_q), .in21(register_21_q),
    .in22(register_22_q), .in23(register_23_q), .in24(register_23_q), .in25(register_25_q),
    .in26(register_26_q), .in27(register_27_q), .in28(register_28_q), .in29(register_29_q),
    .in30(register_30_q), .in31(register_31_q), .out(rs_data), .sel(rs));
  Multiplexer #(.select(5), .width(32)) multiplexer_2 (
    .in0(Zero_Reg_q), .in1(register_1_q), .in2(register_2_q), .in3(register_3_q), .in4(register_4_q),
    .in5(register_5_q), .in6(register_6_q), .in7(register_7_q), .in8(register_8_q), .in9(register_9_q),
    .in10(register_10_q), .in11(register_11_q), .in12(register_12_q), .in13(register_13_q),
    .in14(register_14_q), .in15(register_15_q), .in16(register_16_q), .in17(register_17_q),
    .in18(register_18_q), .in19(register_19_q), .in20(register_20_q), .in21(register_21_q),
    .in22(register_22_q), .in23(register_23_q), .in24(register_23_q), .in25(register_25_q),
    .in26(register_26_q), .in27(register_27_q), .in28(register_28_q), .in29(register_29_q),
    .in30(register_30_q), .in31(register_31_q), .out(rt_data), .sel(rt));
endmodule

module ALU (
  input  [3:0] ALU_CODE,
  input  [31:0] OP1,
  input  [31:0] OP2,
  output Res
);

  Adder adder_1 ();  // open: a, b, out, cin, cout
  Subtractor subtractor_1 ();  // open: a, b, out, bin, bout
  Multiplier multiplier_1 ();  // open: a, b, out, cin, cout
  Divider divider_1 ();  // open: a, b, out, upper, rem
  Register HI ();  // open: D, en, clk, Q, clr
  Register LO ();  // open: D, en, clk, Q, clr
endmodule

module Control (
  input  [31:0] Inst,
  output [4:0] rs,
  output [4:0] rt,
  output [4:0] rd,
  output [31:0] imm,
  output reg_write_e,
  output imm_sel,
  output [3:0] ALU_code
);
endmodule
