// Logisim project Proj3.circ as structural Verilog: 4 circuits, main circuit CPUmain
module CPUmain (
);

  wire clock_1_out, clock_2_out, comparator_1_gt, comparator_2_eq, comparator_3_eq, comparator_4_eq,
       comparator_6_eq, comparator_7_eq, control_1_aluvsmemselect, control_1_imm_sel, control_1_reg_write_e,
       control_1_we_memory, or_1_out, or_2_out, or_3_out, or_4_out;
  wire [3:0] control_1_alu_code, control_1_j_bne_beq;
  wire [4:0] control_1_rd, control_1_rs, control_1_rt;
  wire [15:0] bit_extender_3_out, bit_extender_4_out, shifter_1_out, shifter_2_out, undriven;
  wire [23:0] bit_extender_6_out;
  wire [31:0] adder_1_out, adder_2_out, alu_1_res, bit_extender_1_out, bit_extender_2_out, control_1_imm,
       multiplexer_1_out, multiplexer_2_out, multiplexer_3_out, multiplexer_4_out, multiplexer_5_out,
       multiplexer_6_out, ProgramCounter_q, ram_1_dout, regfile_1_rs_data, regfile_1_rt_data, rom_1_data,
       shifter_3_out, shifter_4_out;

  Shifter #(.width(16)) shifter_1 (.in(undriven), .\dist (4'b0010), .out(shifter_1_out));
  Shifter #(.width(16)) shifter_2 (.in(bit_extender_4_out), .\dist (4'b0010), .out(shifter_2_out));
  Adder #(.width(32)) adder_1 (.a(ProgramCounter_q), .b(32'h4), .out(adder_1_out));  // open: cin, cout
  assign bit_extender_1_out = {{16{shifter_1_out[15]}}, shifter_1_out};  // Bit_Extender bit_extender_1
  assign bit_extender_2_out = {{16{shifter_2_out[15]}}, shifter_2_out};  // Bit_Extender bit_extender_2
  Adder #(.width(32)) adder_2 (.a(adder_1_out), .b(bit_extender_1_out), .out(adder_2_out));  // open: cin, cout
  Multiplexer #(.width(32)) multiplexer_1 (
    .in0(bit_extender_2_out), .in1(regfile_1_rs_data), .out(multiplexer_1_out), .sel(or_3_out));
  Multiplexer #(.width(32)) multiplexer_2 (
    .in0(adder_1_out), .in1(adder_2_out), .out(multiplexer_2_out), .sel(or_1_out));
  Multiplexer #(.width(32)) multiplexer_3 (
    .in0(multiplexer_2_out), .in1(multiplexer_1_out), .out(multiplexer_3_out), .sel(or_4_out));
  Shifter #(.shift("lr"), .width(32)) shifter_3 (.in(ProgramCounter_q), .\dist (5'b00010), .out(shifter_3_out));
  Register #(.width(32)) ProgramCounter (
    .D(multiplexer_3_out), .en(1'b1), .clk(clock_1_out), .Q(ProgramCounter_q));  // open: clr
  Clock clock_1 (.out(clock_1_out));
  ROM #(.addrWidth(16), .dataWidth(32)) rom_1 (.addr(bit_extender_3_out), .data(rom_1_data));
  Bit_Extender #(.in_width(32)) bit_extender_3 (.in(shifter_3_out), .out(bit_extender_3_out));
  Multiplexer #(.width(32)) multiplexer_4 (
    .in0(alu_1_res), .in1(ram_1_dout), .out(multiplexer_4_out), .sel(control_1_aluvsmemselect));
  Bit_Extender #(.in_width(32)) bit_extender_4 (.in(rom_1_data), .out(bit_extender_4_out));
  // Probe on control_1_rs
  // Probe on control_1_rd
  // Probe on rom_1_data
  // Probe on control_1_rt
  Multiplexer #(.width(32)) multiplexer_5 (
    .in0(multiplexer_4_out), .in1(adder_1_out), .out(multiplexer_5_out), .sel(or_2_out));
  or or_1 (or_1_out, comparator_6_eq, comparator_7_eq);
  Comparator #(.width(4)) comparator_1 (.a(control_1_j_bne_beq), .b(4'b0000), .gt(comparator_1_gt));  // open: eq, lt
  Comparator #(.width(4)) comparator_2 (.a(control_1_j_bne_beq), .b(4'b0001), .eq(comparator_2_eq));  // open: gt, lt
  Comparator #(.width(4)) comparator_3 (.a(control_1_j_bne_beq), .b(4'b0010), .eq(comparator_3_eq));  // open: gt, lt
  Comparator #(.width(4)) comparator_4 (.a(control_1_j_bne_beq), .b(4'b0011), .eq(comparator_4_eq));  // open: gt, lt
  Comparator #(.width(4)) comparator_5 (.a(control_1_j_bne_beq), .b(4'b0100));  // open: gt, eq, lt
  regfile regfile_1 (
    .rd_data(multiplexer_5_out), .write_e(control_1_reg_write_e), .rs(control_1_rs), .rd(control_1_rd),
    .rt(control_1_rt), .rs_data(regfile_1_rs_data), .rt_data(regfile_1_rt_data));
  // Probe on regfile_1_rt_data
  Comparator #(.width(4)) comparator_6 (.a(4'b0110), .b(control_1_j_bne_beq), .eq(comparator_6_eq));  // open: gt, lt
  Comparator #(.width(4)) comparator_7 (.a(4'b0101), .b(control_1_j_bne_beq), .eq(comparator_7_eq));  // open: gt, lt
  Control control_1 (
    .Inst(rom_1_data), .ALU_code(control_1_alu_code), .reg_write_e(control_1_reg_write_e),
    .imm_sel(control_1_imm_sel), .ALUvsMemSelect(control_1_aluvsmemselect), .WE_Memory(control_1_we_memory),
    .imm(control_1_imm), .rs(control_1_rs), .rd(control_1_rd), .rt(control_1_rt),
    .j_bne_beq(control_1_j_bne_beq));
  // Probe on regfile_1_rs_data
  or or_2 (or_2_out, comparator_2_eq, comparator_4_eq);
  or or_3 (or_3_out, comparator_3_eq, comparator_4_eq);
  Multiplexer #(.width(32)) multiplexer_6 (
    .in0(regfile_1_rt_data), .in1(control_1_imm), .out(multiplexer_6_out), .sel(control_1_imm_sel));
  assign control_1_imm = {{16{undriven[15]}}, undriven};  // Bit_Extender bit_extender_5
  or or_4 (or_4_out, comparator_1_gt, comparator_2_eq, comparator_3_eq, comparator_4_eq);
  // Probe on control_1_imm_sel
  // Probe on control_1_reg_write_e
  // Probe on control_1_alu_code
  Shifter #(.width(32)) shifter_4 (.in(alu_1_res), .\dist (5'b00010), .out(shifter_4_out));
  ALU alu_1 (.ALU_CODE(control_1_alu_code), .OP1(regfile_1_rs_data), .OP2(multiplexer_6_out), .Res(alu_1_res));
  RAM #(.addrWidth(24), .dataWidth(32), .enables("line")) ram_1 (
    .addr(bit_extender_6_out), .we(control_1_we_memory), .clk(clock_2_out), .din(regfile_1_rt_data),
    .dout(ram_1_dout));
  Bit_Extender #(.in_width(32), .out_width(24)) bit_extender_6 (.in(shifter_4_out), .out(bit_extender_6_out));
  Clock clock_2 (.out(clock_2_out));

  // Notes on the sheet:
  //   PC+4
  //   beq/bne
  //   jr/jalr
  //   contents of rom_1 (hex, n*v repeats v):
  //   2008000a 20090062 95140 9c0c2 1290018 5812 148001a b010 128902a 22d3fffd 2002000a d00c
  //   ALU
  //   PC+4
  //   MEM
  //   j
  //   jal
  //   jr
  //   jalr
  //   syscall
  //   jal/jalr
  //   bne
  //   beq
  //   value from alu
  //   value from mem
endmodule

module regfile (
  input  [31:0] rd_data,
  input  write_e,
  input  [4:0] rs,
  input  [4:0] rd,
  input  [4:0] rt,
  output [31:0] rs_data,
  output [31:0] rt_data
);

  wire clock_1_out, demultiplexer_1_out1, demultiplexer_1_out2, demultiplexer_1_out3, demultiplexer_1_out4,
       demultiplexer_1_out5, demultiplexer_1_out6, demultiplexer_1_out7, demultiplexer_1_out8,
       demultiplexer_1_out9, demultiplexer_1_out10, demultiplexer_1_out11, demultiplexer_1_out12,
       demultiplexer_1_out13, demultiplexer_1_out14, demultiplexer_1_out15, demultiplexer_1_out16,
       demultiplexer_1_out17, demultiplexer_1_out18, demultiplexer_1_out19, demultiplexer_1_out20,
       demultiplexer_1_out21, demultiplexer_1_out22, demultiplexer_1_out23, demultiplexer_1_out24,
       demultiplexer_1_out25, demultiplexer_1_out26, demultiplexer_1_out27, demultiplexer_1_out28,
       demultiplexer_1_out29, demultiplexer_1_out30, demultiplexer_1_out31;
  wire [31:0] register_1_q, register_2_q, register_3_q, register_4_q, register_5_q, register_6_q,
       register_7_q, register_8_q, register_9_q, register_10_q, register_11_q, register_12_q, register_13_q,
       register_14_q, register_15_q, register_16_q, register_17_q, register_18_q, register_19_q,
       register_20_q, register_21_q, register_22_q, register_23_q, register_24_q, register_25_q,
       register_26_q, register_27_q, register_28_q, register_29_q, t2_q, t3_q, Zero_Reg_q;

  Demultiplexer #(.select(5)) demultiplexer_1 (
    .out1(demultiplexer_1_out1), .out2(demultiplexer_1_out2), .out3(demultiplexer_1_out3),
    .out4(demultiplexer_1_out4), .out5(demultiplexer_1_out5), .out6(demultiplexer_1_out6),
    .out7(demultiplexer_1_out7), .out8(demultiplexer_1_out8), .out9(demultiplexer_1_out9),
    .out10(demultiplexer_1_out10), .out11(demultiplexer_1_out11), .out12(demultiplexer_1_out12),
    .out13(demultiplexer_1_out13), .out14(demultiplexer_1_out14), .out15(demultiplexer_1_out15),
    .out16(demultiplexer_1_out16), .out17(demultiplexer_1_out17), .out18(demultiplexer_1_out18),
    .out19(demultiplexer_1_out19), .out20(demultiplexer_1_out20), .out21(demultiplexer_1_out21),
    .out22(demultiplexer_1_out22), .out23(demultiplexer_1_out23), .out24(demultiplexer_1_out24),
    .out25(demultiplexer_1_out25), .out26(demultiplexer_1_out26), .out27(demultiplexer_1_out27),
    .out28(demultiplexer_1_out28), .out29(demultiplexer_1_out29), .out30(demultiplexer_1_out30),
    .out31(demultiplexer_1_out31), .in(write_e), .sel(rd));  // open: out0
  Clock clock_1 (.out(clock_1_out));
  Register #(.width(32)) Zero_Reg (.D({32{1'b0}}), .en(1'b1), .clk(clock_1_out), .Q(Zero_Reg_q));  // open: clr
  Register #(.width(32)) register_1 (
    .D(rd_data), .en(demultiplexer_1_out1), .clk(clock_1_out), .Q(register_1_q));  // open: clr
  Register #(.width(32)) register_2 (
    .D(rd_data), .en(demultiplexer_1_out2), .clk(clock_1_out), .Q(register_2_q));  // open: clr
  Register #(.width(32)) register_3 (
    .D(rd_data), .en(demultiplexer_1_out3), .clk(clock_1_out), .Q(register_3_q));  // open: clr
  Register #(.width(32)) register_4 (
    .D(rd_data), .en(demultiplexer_1_out4), .clk(clock_1_out), .Q(register_4_q));  // open: clr
  Register #(.width(32)) register_5 (
    .D(rd_data), .en(demultiplexer_1_out5), .clk(clock_1_out), .Q(register_5_q));  // open: clr
  Register #(.width(32)) register_6 (
    .D(rd_data), .en(demultiplexer_1_out6), .clk(clock_1_out), .Q(register_6_q));  // open: clr
  Register #(.width(32)) register_7 (
    .D(rd_data), .en(demultiplexer_1_out7), .clk(clock_1_out), .Q(register_7_q));  // open: clr
  Register #(.width(32)) register_8 (
    .D(rd_data), .en(demultiplexer_1_out8), .clk(clock_1_out), .Q(register_8_q));  // open: clr
  Register #(.width(32)) register_9 (
    .D(rd_data), .en(demultiplexer_1_out9), .clk(clock_1_out), .Q(register_9_q));  // open: clr
  Register #(.width(32)) t2 (.D(rd_data), .en(demultiplexer_1_out10), .clk(clock_1_out), .Q(t2_q));  // open: clr
  Register #(.width(32)) t3 (.D(rd_data), .en(demultiplexer_1_out11), .clk(clock_1_out), .Q(t3_q));  // open: clr
  Register #(.width(32)) register_10 (
    .D(rd_data), .en(demultiplexer_1_out12), .clk(clock_1_out), .Q(register_10_q));  // open: clr
  Register #(.width(32)) register_11 (
    .D(rd_data), .en(demultiplexer_1_out13), .clk(clock_1_out), .Q(register_11_q));  // open: clr
  Register #(.width(32)) register_12 (
    .D(rd_data), .en(demultiplexer_1_out14), .clk(clock_1_out), .Q(register_12_q));  // open: clr
  Register #(.width(32)) register_13 (
    .D(rd_data), .en(demultiplexer_1_out15), .clk(clock_1_out), .Q(register_13_q));  // open: clr
  Register #(.width(32)) register_14 (
    .D(rd_data), .en(demultiplexer_1_out16), .clk(clock_1_out), .Q(register_14_q));  // open: clr
  Register #(.width(32)) register_15 (
    .D(rd_data), .en(demultiplexer_1_out17), .clk(clock_1_out), .Q(register_15_q));  // open: clr
  Register #(.width(32)) register_16 (
    .D(rd_data), .en(demultiplexer_1_out18), .clk(clock_1_out), .Q(register_16_q));  // open: clr
  Register #(.width(32)) register_17 (
    .D(rd_data), .en(demultiplexer_1_out19), .clk(clock_1_out), .Q(register_17_q));  // open: clr
  Register #(.width(32)) register_18 (
    .D(rd_data), .en(demultiplexer_1_out20), .clk(clock_1_out), .Q(register_18_q));  // open: clr
  Register #(.width(32)) register_19 (
    .D(rd_data), .en(demultiplexer_1_out21), .clk(clock_1_out), .Q(register_19_q));  // open: clr
  Register #(.width(32)) register_20 (
    .D(rd_data), .en(demultiplexer_1_out22), .clk(clock_1_out), .Q(register_20_q));  // open: clr
  Register #(.width(32)) register_21 (
    .D(rd_data), .en(demultiplexer_1_out23), .clk(clock_1_out), .Q(register_21_q));  // open: clr
  Register #(.width(32)) register_22 (
    .D(rd_data), .en(demultiplexer_1_out24), .clk(clock_1_out), .Q(register_22_q));  // open: clr
  Register #(.width(32)) register_23 (
    .D(rd_data), .en(demultiplexer_1_out25), .clk(clock_1_out), .Q(register_23_q));  // open: clr
  Register #(.width(32)) register_24 (
    .D(rd_data), .en(demultiplexer_1_out26), .clk(clock_1_out), .Q(register_24_q));  // open: clr
  Register #(.width(32)) register_25 (
    .D(rd_data), .en(demultiplexer_1_out27), .clk(clock_1_out), .Q(register_25_q));  // open: clr
  Register #(.width(32)) register_26 (
    .D(rd_data), .en(demultiplexer_1_out28), .clk(clock_1_out), .Q(register_26_q));  // open: clr
  Register #(.width(32)) register_27 (
    .D(rd_data), .en(demultiplexer_1_out29), .clk(clock_1_out), .Q(register_27_q));  // open: clr
  Register #(.width(32)) register_28 (
    .D(rd_data), .en(demultiplexer_1_out30), .clk(clock_1_out), .Q(register_28_q));  // open: clr
  Register #(.width(32)) register_29 (
    .D(rd_data), .en(demultiplexer_1_out31), .clk(clock_1_out), .Q(register_29_q));  // open: clr
  Multiplexer #(.select(5), .width(32)) multiplexer_1 (
    .in0(Zero_Reg_q), .in1(register_1_q), .in2(register_2_q), .in3(register_3_q), .in4(register_4_q),
    .in5(register_5_q), .in6(register_6_q), .in7(register_7_q), .in8(register_8_q), .in9(register_9_q),
    .in10(t2_q), .in11(t3_q), .in12(register_10_q), .in13(register_11_q), .in14(register_12_q),
    .in15(register_13_q), .in16(register_14_q), .in17(register_15_q), .in18(register_16_q),
    .in19(register_17_q), .in20(register_18_q), .in21(register_19_q), .in22(register_20_q),
    .in23(register_21_q), .in24(register_22_q), .in25(register_23_q), .in26(register_24_q),
    .in27(register_25_q), .in28(register_26_q), .in29(register_27_q), .in30(register_28_q),
    .in31(register_29_q), .out(rs_data), .sel(rs));
  Multiplexer #(.select(5), .width(32)) multiplexer_2 (
    .in0(Zero_Reg_q), .in1(register_1_q), .in2(register_2_q), .in3(register_3_q), .in4(register_4_q),
    .in5(register_5_q), .in6(register_6_q), .in7(register_7_q), .in8(register_8_q), .in9(register_9_q),
    .in10(t2_q), .in11(t3_q), .in12(register_10_q), .in13(register_11_q), .in14(register_12_q),
    .in15(register_13_q), .in16(register_14_q), .in17(register_15_q), .in18(register_16_q),
    .in19(register_17_q), .in20(register_18_q), .in21(register_19_q), .in22(register_20_q),
    .in23(register_21_q), .in24(register_22_q), .in25(register_23_q), .in26(register_24_q),
    .in27(register_25_q), .in28(register_26_q), .in29(register_27_q), .in30(register_28_q),
    .in31(register_29_q), .out(rt_data), .sel(rt));
endmodule

module ALU (
  input  [3:0] ALU_CODE,
  input  [31:0] OP1,
  input  [31:0] OP2,
  output [31:0] Res
);

  wire and_1_out, bit_extender_3_out, bit_extender_4_out, bit_extender_5_out, bit_extender_6_out,
       bit_extender_7_out, bit_extender_8_out, bit_extender_9_out, bit_extender_10_out, clock_1_out,
       comparator_1_lt, comparator_2_eq, comparator_3_eq, comparator_4_eq, comparator_5_eq, comparator_6_eq,
       comparator_7_eq, comparator_8_eq, comparator_9_eq, comparator_10_eq, comparator_11_eq,
       comparator_12_eq, comparator_13_eq, nor_1_out, or_1_out, or_2_out, xor_1_out;
  wire [1:0] multiplexer_11_out, multiplexer_11_out_2, multiplexer_13_out, multiplexer_13_out_2,
       multiplexer_16_out, multiplexer_18_out;
  wire [4:0] bit_extender_1_out, bit_extender_2_out;
  wire [7:0] multiplexer_7_out, multiplexer_9_out;
  wire [15:0] multiplexer_1_out, multiplexer_3_out;
  wire [31:0] adder_1_out, adder_2_out, adder_3_out, adder_4_out, adder_5_out, adder_6_out, adder_7_out,
       adder_8_out, adder_9_out, adder_10_out, adder_11_out, bit_extender_11_out, bit_extender_12_out,
       bit_extender_13_out, bit_extender_14_out, bit_extender_15_out, divider_1_out, divider_1_rem, HI_q,
       LO_q, multiplexer_2_out, multiplexer_4_out, multiplexer_5_out, multiplexer_6_out, multiplexer_8_out,
       multiplexer_10_out, multiplexer_12_out, multiplexer_14_out, multiplexer_17_out, multiplexer_19_out,
       multiplexer_21_out, multiplexer_23_out, multiplier_1_cout, multiplier_1_out, shifter_1_out,
       shifter_2_out, shifter_3_out, subtractor_1_out;

  Bit_Extender #(.in_width(32), .out_width(5)) bit_extender_1 (.in(OP2), .out(bit_extender_1_out));
  Bit_Extender #(.in_width(32), .out_width(5)) bit_extender_2 (.in(OP2), .out(bit_extender_2_out));
  Bit_Extender #(.in_width(32), .out_width(1)) bit_extender_3 (.in(OP1), .out(bit_extender_3_out));
  Bit_Extender #(.in_width(32), .out_width(1)) bit_extender_4 (.in(OP2), .out(bit_extender_4_out));
  Bit_Extender #(.in_width(32), .out_width(1)) bit_extender_5 (.in(OP1), .out(bit_extender_5_out));
  Bit_Extender #(.in_width(32), .out_width(1)) bit_extender_6 (.in(OP2), .out(bit_extender_6_out));
  Bit_Extender #(.in_width(32), .out_width(1)) bit_extender_7 (.in(OP1), .out(bit_extender_7_out));
  Bit_Extender #(.in_width(32), .out_width(1)) bit_extender_8 (.in(OP2), .out(bit_extender_8_out));
  Bit_Extender #(.in_width(32), .out_width(1)) bit_extender_9 (.in(OP1), .out(bit_extender_9_out));
  Bit_Extender #(.in_width(32), .out_width(1)) bit_extender_10 (.in(OP2), .out(bit_extender_10_out));
  Adder #(.width(32)) adder_1 (.a(OP1), .b(OP2), .out(adder_1_out));  // open: cin, cout
  Subtractor #(.width(32)) subtractor_1 (.a(OP1), .b(OP2), .out(subtractor_1_out));  // open: bin, bout
  Multiplier #(.width(32)) multiplier_1 (
    .a(OP1), .b(OP2), .out(multiplier_1_out), .cout(multiplier_1_cout));  // open: cin
  Divider #(.width(32)) divider_1 (.a(OP1), .b(OP2), .out(divider_1_out), .rem(divider_1_rem));  // open: upper
  Shifter #(.width(32)) shifter_1 (.in(OP1), .\dist (bit_extender_1_out), .out(shifter_1_out));
  Shifter #(.shift("lr"), .width(32)) shifter_2 (.in(OP2), .\dist (bit_extender_2_out), .out(shifter_2_out));
  Comparator #(.width(32)) comparator_1 (.a(OP1), .b(OP2), .lt(comparator_1_lt));  // open: gt, eq
  and and_1 (and_1_out, bit_extender_3_out, bit_extender_4_out);
  or or_1 (or_1_out, bit_extender_5_out, bit_extender_6_out);
  nor nor_1 (nor_1_out, bit_extender_7_out, bit_extender_8_out);
  xor xor_1 (xor_1_out, bit_extender_9_out, bit_extender_10_out);
  Shifter #(.width(32)) shifter_3 (.in(OP2), .\dist (5'b10000), .out(shifter_3_out));
  Comparator #(.width(16)) comparator_2 (.a(OP1[31:16]), .b(16'h1), .eq(comparator_2_eq));  // open: gt, lt
  Comparator #(.width(16)) comparator_3 (.a(OP1[31:16]), .b({16{1'b0}}), .eq(comparator_3_eq));  // open: gt, lt
  assign bit_extender_11_out = {{31{comparator_1_lt}}, comparator_1_lt};  // Bit_Extender bit_extender_11
  assign bit_extender_12_out = {{31{and_1_out}}, and_1_out};  // Bit_Extender bit_extender_12
  assign bit_extender_13_out = {{31{or_1_out}}, or_1_out};  // Bit_Extender bit_extender_13
  assign bit_extender_14_out = {{31{nor_1_out}}, nor_1_out};  // Bit_Extender bit_extender_14
  assign bit_extender_15_out = {{31{xor_1_out}}, xor_1_out};  // Bit_Extender bit_extender_15
  Multiplexer #(.width(16)) multiplexer_1 (
    .in0(OP1[31:16]), .in1(OP1[15:0]), .out(multiplexer_1_out), .sel(comparator_2_eq));
  Multiplexer #(.width(32)) multiplexer_2 (
    .in0({32{1'b0}}), .in1(32'h10), .out(multiplexer_2_out), .sel(comparator_2_eq));
  Multiplexer #(.width(16)) multiplexer_3 (
    .in0(OP1[31:16]), .in1(OP1[15:0]), .out(multiplexer_3_out), .sel(comparator_3_eq));
  Multiplexer #(.width(32)) multiplexer_4 (
    .in0({32{1'b0}}), .in1(32'h10), .out(multiplexer_4_out), .sel(comparator_3_eq));
  Comparator #(.width(4)) comparator_4 (.a(ALU_CODE), .b(4'b0010), .eq(comparator_4_eq));  // open: gt, lt
  Comparator #(.width(4)) comparator_5 (.a(ALU_CODE), .b(4'b0011), .eq(comparator_5_eq));  // open: gt, lt
  Multiplexer #(.width(32)) multiplexer_5 (
    .in0(multiplier_1_cout), .in1(divider_1_rem), .out(multiplexer_5_out), .sel(comparator_5_eq));
  Multiplexer #(.width(32)) multiplexer_6 (
    .in0(multiplier_1_out), .in1(divider_1_out), .out(multiplexer_6_out), .sel(comparator_5_eq));
  Adder #(.width(32)) adder_2 (.a({32{1'b0}}), .b(multiplexer_2_out), .out(adder_2_out));  // open: cin, cout
  Adder #(.width(32)) adder_3 (.a({32{1'b0}}), .b(multiplexer_4_out), .out(adder_3_out));  // open: cin, cout
  Register #(.width(32)) HI (.D(multiplexer_5_out), .en(or_2_out), .clk(clock_1_out), .Q(HI_q));  // open: clr
  Register #(.width(32)) LO (.D(multiplexer_6_out), .en(or_2_out), .clk(clock_1_out), .Q(LO_q));  // open: clr
  Clock clock_1 (.out(clock_1_out));
  Multiplexer #(.width(8)) multiplexer_7 (
    .in0(multiplexer_1_out[15:8]), .in1(multiplexer_1_out[7:0]), .out(multiplexer_7_out),
    .sel(comparator_6_eq));
  Comparator comparator_6 (.a(multiplexer_1_out[15:8]), .b(8'h1), .eq(comparator_6_eq));  // open: gt, lt
  Multiplexer #(.width(32)) multiplexer_8 (
    .in0({32{1'b0}}), .in1(32'h8), .out(multiplexer_8_out), .sel(comparator_6_eq));
  Multiplexer #(.width(8)) multiplexer_9 (
    .in0(multiplexer_3_out[15:8]), .in1(multiplexer_3_out[7:0]), .out(multiplexer_9_out),
    .sel(comparator_7_eq));
  Comparator comparator_7 (.a(multiplexer_3_out[15:8]), .b({8{1'b0}}), .eq(comparator_7_eq));  // open: gt, lt
  Multiplexer #(.width(32)) multiplexer_10 (
    .in0({32{1'b0}}), .in1(32'h8), .out(multiplexer_10_out), .sel(comparator_7_eq));
  or or_2 (or_2_out, comparator_4_eq, comparator_5_eq);
  Adder #(.width(32)) adder_4 (.a(multiplexer_8_out), .b(adder_2_out), .out(adder_4_out));  // open: cin, cout
  Adder #(.width(32)) adder_5 (.a(multiplexer_10_out), .b(adder_3_out), .out(adder_5_out));  // open: cin, cout
  Comparator #(.width(4)) comparator_8 (.a(multiplexer_7_out[7:4]), .b(4'b0001), .eq(comparator_8_eq));  // open: gt, lt
  Adder #(.width(32)) adder_6 (.a(multiplexer_12_out), .b(adder_4_out), .out(adder_6_out));  // open: cin, cout
  Comparator #(.width(4)) comparator_9 (.a(multiplexer_9_out[7:4]), .b(4'b0000), .eq(comparator_9_eq));  // open: gt, lt
  Adder #(.width(32)) adder_7 (.a(multiplexer_14_out), .b(adder_5_out), .out(adder_7_out));  // open: cin, cout
  Multiplexer #(.width(4)) multiplexer_11 (
    .in0(multiplexer_7_out[7:4]), .in1(multiplexer_7_out[3:0]),
    .out({multiplexer_11_out_2, multiplexer_11_out}), .sel(comparator_8_eq));
  Multiplexer #(.width(32)) multiplexer_12 (
    .in0({32{1'b0}}), .in1(32'h4), .out(multiplexer_12_out), .sel(comparator_8_eq));
  Multiplexer #(.width(4)) multiplexer_13 (
    .in0(multiplexer_9_out[7:4]), .in1(multiplexer_9_out[3:0]),
    .out({multiplexer_13_out_2, multiplexer_13_out}), .sel(comparator_9_eq));
  Multiplexer #(.width(32)) multiplexer_14 (
    .in0({32{1'b0}}), .in1(32'h4), .out(multiplexer_14_out), .sel(comparator_9_eq));
  Multiplexer #(.select(4), .width(32)) multiplexer_15 (
    .in0(adder_1_out), .in1(subtractor_1_out), .in4(LO_q), .in5(HI_q), .in6(shifter_1_out),
    .in7(shifter_2_out), .in8(bit_extender_11_out), .in9(bit_extender_12_out), .in10(bit_extender_13_out),
    .in11(bit_extender_14_out), .in12(bit_extender_15_out), .in13(shifter_3_out), .in14(adder_10_out),
    .in15(adder_11_out), .out(Res), .sel(ALU_CODE));  // open: in2, in3
  Comparator #(.width(2)) comparator_10 (.a(multiplexer_11_out_2), .b(2'b01), .eq(comparator_10_eq));  // open: gt, lt
  Adder #(.width(32)) adder_8 (.a(multiplexer_17_out), .b(adder_6_out), .out(adder_8_out));  // open: cin, cout
  Comparator #(.width(2)) comparator_11 (.a(multiplexer_13_out_2), .b(2'b00), .eq(comparator_11_eq));  // open: gt, lt
  Adder #(.width(32)) adder_9 (.a(multiplexer_19_out), .b(adder_7_out), .out(adder_9_out));  // open: cin, cout
  Multiplexer #(.width(2)) multiplexer_16 (
    .in0(multiplexer_11_out_2), .in1(multiplexer_11_out), .out(multiplexer_16_out), .sel(comparator_10_eq));
  Multiplexer #(.width(32)) multiplexer_17 (
    .in0({32{1'b0}}), .in1(32'h2), .out(multiplexer_17_out), .sel(comparator_10_eq));
  Multiplexer #(.width(2)) multiplexer_18 (
    .in0(multiplexer_13_out_2), .in1(multiplexer_13_out), .out(multiplexer_18_out), .sel(comparator_11_eq));
  Multiplexer #(.width(32)) multiplexer_19 (
    .in0({32{1'b0}}), .in1(32'h2), .out(multiplexer_19_out), .sel(comparator_11_eq));
  Comparator #(.width(1)) comparator_12 (.a(multiplexer_16_out[1]), .b(1'b1), .eq(comparator_12_eq));  // open: gt, lt
  Adder #(.width(32)) adder_10 (.a(multiplexer_21_out), .b(adder_8_out), .out(adder_10_out));  // open: cin, cout
  Adder #(.width(32)) adder_11 (.a(multiplexer_23_out), .b(adder_9_out), .out(adder_11_out));  // open: cin, cout
  Multiplexer multiplexer_20 (
    .in0(multiplexer_16_out[1]), .in1(multiplexer_16_out[0]), .sel(comparator_12_eq));  // open: out
  Multiplexer #(.width(32)) multiplexer_21 (
    .in0({32{1'b0}}), .in1(32'h1), .out(multiplexer_21_out), .sel(comparator_12_eq));
  Multiplexer multiplexer_22 (
    .in0(multiplexer_18_out[1]), .in1(multiplexer_18_out[0]), .sel(comparator_13_eq));  // open: out
  Comparator #(.width(1)) comparator_13 (.a(multiplexer_18_out[1]), .b(1'b0), .eq(comparator_13_eq));  // open: gt, lt
  Multiplexer #(.width(32)) multiplexer_23 (
    .in0({32{1'b0}}), .in1(32'h1), .out(multiplexer_23_out), .sel(comparator_13_eq));

  // Notes on the sheet:
  //   clo
  //   clz
  //   Add
  //   Sub
  //   sll
  //   srl
  //   slt
  //   lui
  //   Upper
  //   Lower
  //   mult
  //   div
endmodule

module Control (
  input  [31:0] Inst,
  output [3:0] ALU_code,
  output reg_write_e,
  output imm_sel,
  output ALUvsMemSelect,
  output WE_Memory,
  output [31:0] imm,
  output [4:0] rs,
  output [4:0] rd,
  output [4:0] rt,
  output [3:0] j_bne_beq
);

  wire and1_out, clo_out, clz_out, comparator_1_eq, comparator_2_eq, comparator_3_eq, comparator_4_eq,
       comparator_5_eq, comparator_6_eq, comparator_7_eq, comparator_8_eq, comparator_9_eq, comparator_10_eq,
       comparator_11_eq, comparator_12_eq, comparator_13_eq, comparator_14_eq, comparator_15_eq,
       comparator_16_eq, comparator_17_eq, comparator_18_eq, comparator_19_eq, comparator_22_eq,
       comparator_23_eq, comparator_24_eq, comparator_25_eq, comparator_26_eq, comparator_27_eq,
       comparator_28_eq, comparator_29_eq, comparator_30_eq, comparator_31_eq, comparator_32_eq,
       comparator_33_eq, comparator_34_eq, comparator_35_eq, comparator_36_eq, comparator_37_eq,
       comparator_38_eq, comparator_39_eq, comparator_40_eq, comparator_41_eq, comparator_42_eq,
       comparator_43_eq, comparator_44_eq, comparator_45_eq, comparator_46_eq, comparator_47_eq, div_out,
       jalr_out, jr_out, mfhi_out, mflo_out, mult_out, nor1_out, or1_out, or_1_out, or_11_out, sll1_out,
       slt_out, srl1_out, sub_out, xor1_out;
  wire [1:0] shamt_out;
  wire [2:0] or_9_out;
  wire [20:0] bit_extender_1_out, bit_extender_2_out, multiplexer_3_out;

  Comparator #(.mode("unsigned"), .width(6)) comparator_1 (
    .a(Inst[5:0]), .b(6'b100000), .eq(comparator_1_eq));  // open: gt, lt
  Comparator #(.width(6)) comparator_2 (.a(Inst[31:26]), .b({6{1'b0}}), .eq(comparator_2_eq));  // open: gt, lt
  Comparator #(.width(6)) comparator_3 (.a(Inst[31:26]), .b(6'b001000), .eq(comparator_3_eq));  // open: gt, lt
  Comparator #(.mode("unsigned"), .width(6)) comparator_4 (
    .a(Inst[5:0]), .b(6'b100010), .eq(comparator_4_eq));  // open: gt, lt
  Comparator #(.width(6)) comparator_5 (.a(Inst[31:26]), .b({6{1'b0}}), .eq(comparator_5_eq));  // open: gt, lt
  Comparator #(.mode("unsigned"), .width(6)) comparator_6 (
    .a(Inst[5:0]), .b(6'b011000), .eq(comparator_6_eq));  // open: gt, lt
  Comparator #(.width(6)) comparator_7 (.a(Inst[31:26]), .b({6{1'b0}}), .eq(comparator_7_eq));  // open: gt, lt
  Comparator #(.mode("unsigned"), .width(6)) comparator_8 (
    .a(Inst[5:0]), .b(6'b011010), .eq(comparator_8_eq));  // open: gt, lt
  Comparator #(.width(6)) comparator_9 (.a(Inst[31:26]), .b({6{1'b0}}), .eq(comparator_9_eq));  // open: gt, lt
  Comparator #(.mode("unsigned"), .width(6)) comparator_10 (
    .a(Inst[5:0]), .b(6'b010010), .eq(comparator_10_eq));  // open: gt, lt
  Comparator #(.width(6)) comparator_11 (.a(Inst[31:26]), .b({6{1'b0}}), .eq(comparator_11_eq));  // open: gt, lt
  Comparator #(.mode("unsigned"), .width(6)) comparator_12 (
    .a(Inst[5:0]), .b(6'b010000), .eq(comparator_12_eq));  // open: gt, lt
  Comparator #(.width(6)) comparator_13 (.a(Inst[31:26]), .b({6{1'b0}}), .eq(comparator_13_eq));  // open: gt, lt
  Comparator #(.mode("unsigned"), .width(6)) comparator_14 (
    .a(Inst[5:0]), .b(6'b101010), .eq(comparator_14_eq));  // open: gt, lt
  Comparator #(.width(6)) comparator_15 (.a(Inst[31:26]), .b({6{1'b0}}), .eq(comparator_15_eq));  // open: gt, lt
  Comparator #(.mode("unsigned"), .width(6)) comparator_16 (
    .a(Inst[5:0]), .b({6{1'b0}}), .eq(comparator_16_eq));  // open: gt, lt
  Comparator #(.width(6)) comparator_17 (.a(Inst[31:26]), .b({6{1'b0}}), .eq(comparator_17_eq));  // open: gt, lt
  Comparator #(.mode("unsigned"), .width(6)) comparator_18 (
    .a(Inst[5:0]), .b(6'b000010), .eq(comparator_18_eq));  // open: gt, lt
  Comparator #(.width(6)) comparator_19 (.a(Inst[31:26]), .b({6{1'b0}}), .eq(comparator_19_eq));  // open: gt, lt
  Comparator #(.width(6)) comparator_20 (.a(Inst[31:26]), .b(6'b100011), .eq(ALUvsMemSelect));  // open: gt, lt
  Comparator #(.width(6)) comparator_21 (.a(Inst[31:26]), .b(6'b101011), .eq(WE_Memory));  // open: gt, lt
  Comparator #(.width(6)) comparator_22 (.a(Inst[31:26]), .b(6'b000100), .eq(comparator_22_eq));  // open: gt, lt
  Comparator #(.width(6)) comparator_23 (.a(Inst[31:26]), .b(6'b000101), .eq(comparator_23_eq));  // open: gt, lt
  Comparator #(.width(6)) comparator_24 (.a(Inst[5:0]), .b(6'b100100), .eq(comparator_24_eq));  // open: gt, lt
  Comparator #(.width(6)) comparator_25 (.a(Inst[31:26]), .b({6{1'b0}}), .eq(comparator_25_eq));  // open: gt, lt
  Comparator #(.width(6)) comparator_26 (.a(Inst[5:0]), .b(6'b100101), .eq(comparator_26_eq));  // open: gt, lt
  Comparator #(.width(6)) comparator_27 (.a(Inst[31:26]), .b(6'b001000), .eq(comparator_27_eq));  // open: gt, lt
  Comparator #(.width(6)) comparator_28 (.a(Inst[5:0]), .b(6'b100111), .eq(comparator_28_eq));  // open: gt, lt
  Comparator #(.width(6)) comparator_29 (.a(Inst[31:26]), .b({6{1'b0}}), .eq(comparator_29_eq));  // open: gt, lt
  Comparator #(.width(6)) comparator_30 (.a(Inst[5:0]), .b(6'b100110), .eq(comparator_30_eq));  // open: gt, lt
  Comparator #(.width(6)) comparator_31 (.a(Inst[31:26]), .b({6{1'b0}}), .eq(comparator_31_eq));  // open: gt, lt
  Comparator #(.width(6)) comparator_32 (.a(Inst[31:26]), .b(6'b001100), .eq(comparator_32_eq));  // open: gt, lt
  Comparator #(.width(6)) comparator_33 (.a(Inst[31:26]), .b(6'b001101), .eq(comparator_33_eq));  // open: gt, lt
  Comparator #(.width(6)) comparator_34 (.a(Inst[31:26]), .b(6'b001110), .eq(comparator_34_eq));  // open: gt, lt
  Comparator #(.width(6)) comparator_35 (.a(Inst[31:26]), .b(6'b001111), .eq(comparator_35_eq));  // open: gt, lt
  Comparator #(.width(6)) comparator_36 (.a(Inst[5:0]), .b(6'b100001), .eq(comparator_36_eq));  // open: gt, lt
  Comparator #(.width(6)) comparator_37 (.a(Inst[31:26]), .b(6'b011100), .eq(comparator_37_eq));  // open: gt, lt
  Comparator #(.width(6)) comparator_38 (.a(Inst[5:0]), .b(6'b100000), .eq(comparator_38_eq));  // open: gt, lt
  Comparator #(.width(6)) comparator_39 (.a(Inst[31:26]), .b(6'b011100), .eq(comparator_39_eq));  // open: gt, lt
  Comparator #(.width(6)) comparator_40 (.a(Inst[31:26]), .b(6'b000010), .eq(comparator_40_eq));  // open: gt, lt
  Comparator #(.width(6)) comparator_41 (.a(Inst[31:26]), .b(6'b000011), .eq(comparator_41_eq));  // open: gt, lt
  Comparator #(.width(6)) comparator_42 (.a(Inst[5:0]), .b(6'b001000), .eq(comparator_42_eq));  // open: gt, lt
  Comparator #(.width(6)) comparator_43 (.a(Inst[31:26]), .b({6{1'b0}}), .eq(comparator_43_eq));  // open: gt, lt
  Comparator #(.width(6)) comparator_44 (.a(Inst[5:0]), .b(6'b001001), .eq(comparator_44_eq));  // open: gt, lt
  Comparator #(.width(6)) comparator_45 (.a(Inst[31:26]), .b({6{1'b0}}), .eq(comparator_45_eq));  // open: gt, lt
  Comparator #(.width(6)) comparator_46 (.a(Inst[5:0]), .b(6'b001100), .eq(comparator_46_eq));  // open: gt, lt
  Comparator #(.width(6)) comparator_47 (.a(Inst[31:26]), .b({6{1'b0}}), .eq(comparator_47_eq));  // open: gt, lt
  // AND_Gate add has open pins: in0=comparator_1_eq, in1=comparator_2_eq, out=open
  and sub (sub_out, comparator_4_eq, comparator_5_eq);
  and mult (mult_out, comparator_6_eq, comparator_7_eq);
  and div (div_out, comparator_8_eq, comparator_9_eq);
  and mflo (mflo_out, comparator_10_eq, comparator_11_eq);
  and mfhi (mfhi_out, comparator_12_eq, comparator_13_eq);
  and slt (slt_out, comparator_14_eq, comparator_15_eq);
  and sll1 (sll1_out, comparator_16_eq, comparator_17_eq);
  and srl1 (srl1_out, comparator_18_eq, comparator_19_eq);
  and and1 (and1_out, comparator_24_eq, comparator_25_eq);
  and or1 (or1_out, comparator_26_eq, comparator_27_eq);
  and nor1 (nor1_out, comparator_28_eq, comparator_29_eq);
  and xor1 (xor1_out, comparator_30_eq, comparator_31_eq);
  and clo (clo_out, comparator_36_eq, comparator_37_eq);
  and clz (clz_out, comparator_38_eq, comparator_39_eq);
  and jr (jr_out, comparator_42_eq, comparator_43_eq);
  and jalr (jalr_out, comparator_44_eq, comparator_45_eq);
  and syscall (or_9_out[2], comparator_46_eq, comparator_47_eq);
  or or_1 (or_1_out, clo_out, clz_out, jr_out, jalr_out, or_9_out[2]);
  or or_2 (ALU_code[0], comparator_22_eq, sub_out, div_out, mfhi_out, srl1_out, and1_out, nor1_out, comparator_32_eq, comparator_35_eq, clz_out, comparator_23_eq);
  Multiplexer #(.width(5)) multiplexer_1 (.in0(Inst[20:16]), .in1({5{1'b0}}), .out(rt), .sel(or_1_out));
  or or_3 (ALU_code[1], mult_out, div_out, sll1_out, srl1_out, or1_out, nor1_out, comparator_33_eq, clo_out, clz_out);
  or or_4 (j_bne_beq[1], comparator_23_eq, jr_out, jalr_out);
  or or_5 (ALU_code[2], mflo_out, mfhi_out, sll1_out, srl1_out, xor1_out, comparator_34_eq, comparator_35_eq, clo_out, clz_out);
  or or_6 (j_bne_beq[0], comparator_22_eq, comparator_41_eq, jalr_out);
  or or_7 (j_bne_beq[2], comparator_22_eq, comparator_23_eq, or_9_out[2]);
  or or_8 (ALU_code[3], slt_out, and1_out, or1_out, nor1_out, xor1_out, comparator_32_eq, comparator_33_eq, comparator_34_eq, comparator_35_eq, clo_out, clz_out);
  or or_9 (or_9_out[0], mult_out, div_out);
  or or_10 (or_9_out[1], comparator_3_eq, ALUvsMemSelect, WE_Memory, comparator_22_eq, comparator_23_eq, comparator_32_eq, comparator_33_eq, comparator_34_eq, comparator_35_eq, comparator_41_eq);
  Multiplexer multiplexer_2 (.in0(1'b1), .in1(1'b0), .out(reg_write_e), .sel(or_11_out));
  or or_11 (or_11_out, mult_out, div_out, WE_Memory, comparator_22_eq, comparator_23_eq);
  or or_12 (imm_sel, comparator_3_eq, ALUvsMemSelect, WE_Memory, sll1_out, srl1_out, comparator_32_eq, comparator_33_eq, comparator_34_eq, clo_out);
  assign bit_extender_1_out = {{5{Inst[15]}}, Inst[15:0]};  // Bit_Extender bit_extender_1
  assign bit_extender_2_out = {{16{Inst[10]}}, Inst[10:6]};  // Bit_Extender bit_extender_2
  // Probe on reg_write_e
  // Probe on or_11_out
  or shamt (shamt_out[0], sll1_out, srl1_out);
  Multiplexer #(.select(2), .width(21)) multiplexer_3 (
    .in0(bit_extender_1_out), .in1(bit_extender_2_out), .in2(Inst[20:0]), .out(multiplexer_3_out),
    .sel(shamt_out));  // open: in3
  or or_13 (shamt_out[1], comparator_41_eq, comparator_40_eq);
  Multiplexer #(.select(3), .width(5)) multiplexer_4 (
    .in0(Inst[15:11]), .in1({5{1'b0}}), .in2(Inst[20:16]), .in3({5{1'b1}}), .in4(5'b01010), .out(rd),
    .sel(or_9_out));  // open: in5, in6, in7
  assign imm = {{11{multiplexer_3_out[20]}}, multiplexer_3_out};  // Bit_Extender bit_extender_3

  assign j_bne_beq[3] = 1'b0;
  assign rs = Inst[25:21];

  // Notes on the sheet:
  //   Inst: initial=0x12a4020
  //   Func code
  //   Op code
  //   5:0
  //   25:21
  //   Func and Op codes in Hex
  //   15:11
  //   20:16
  //   addi
  //   lw
  //   beq
  //   bne
  //   andi
  //   ori
  //   xori
  //   lui
  //   10:6
  //   j
  //   jal
  //   sw
endmodule
