// Logisim project Proj4_ID_added_controllers.circ as structural Verilog: 10 circuits, main circuit Computer
module CPUmain (
  output [25:0] Address,
  output BusWriteEnable,
  output [31:0] DataToBus,
  output [31:0] DataFromBus
);

  wire alu_1_equal, and_1_out, and_2_out, clock_1_out, comparator_1_eq, comparator_2_eq, comparator_3_eq,
       comparator_4_eq, comparator_6_eq, comparator_7_eq, comparator_8_eq, comparator_9_eq,
       control_1_aluvsmemselect, control_1_imm_sel, control_1_reg_write_e, not_1_out, or_1_out, or_2_out,
       or_3_out, or_4_out, or_5_out;
  wire [3:0] control_1_alu_code, control_1_j_bne_beq;
  wire [4:0] control_1_rd, control_1_rs, control_1_rt;
  wire [15:0] bit_extender_2_out;
  wire [25:0] bit_extender_3_out, shifter_2_out;
  wire [31:0] adder_1_out, adder_2_out, alu_1_res, bit_extender_1_out, control_1_imm, multiplexer_1_out,
       multiplexer_2_out, multiplexer_3_out, multiplexer_4_out, multiplexer_5_out, multiplexer_6_out,
       multiplexer_7_out, multiplexer_8_out, ProgramCounter_q, regfile_1_rs_data, rom_1_data, shifter_1_out,
       shifter_3_out, shifter_4_out;

  Shifter #(.width(32)) shifter_1 (.in(control_1_imm), .\dist (5'b00010), .out(shifter_1_out));
  Shifter #(.width(26)) shifter_2 (.in(bit_extender_3_out), .\dist (5'b00010), .out(shifter_2_out));
  // Probe on ProgramCounter_q
  Adder #(.width(32)) adder_1 (.a(ProgramCounter_q), .b(32'h4), .out(adder_1_out));  // open: cin, cout
  assign bit_extender_1_out = {{6{shifter_2_out[25]}}, shifter_2_out};  // Bit_Extender bit_extender_1
  Adder #(.width(32)) adder_2 (.a(adder_1_out), .b(shifter_1_out), .out(adder_2_out));  // open: cin, cout
  // Probe on adder_2_out
  Multiplexer #(.width(32)) multiplexer_1 (
    .in0(bit_extender_1_out), .in1(regfile_1_rs_data), .out(multiplexer_1_out), .sel(or_3_out));
  Multiplexer #(.width(32)) multiplexer_2 (
    .in0(adder_1_out), .in1(adder_2_out), .out(multiplexer_2_out), .sel(or_1_out));
  Multiplexer #(.width(32)) multiplexer_3 (
    .in0(multiplexer_2_out), .in1(multiplexer_1_out), .out(multiplexer_3_out), .sel(or_4_out));
  Shifter #(.shift("lr"), .width(32)) shifter_3 (.in(ProgramCounter_q), .\dist (5'b00010), .out(shifter_3_out));
  Register #(.width(32)) ProgramCounter (
    .D(multiplexer_3_out), .en(1'b1), .clk(clock_1_out), .Q(ProgramCounter_q));  // open: clr
  Clock clock_1 (.out(clock_1_out));
  ROM #(.addrWidth(16), .dataWidth(32)) rom_1 (.addr(bit_extender_2_out), .data(rom_1_data));
  Bit_Extender #(.in_width(32)) bit_extender_2 (.in(shifter_3_out), .out(bit_extender_2_out));
  or or_1 (or_1_out, and_1_out, and_2_out);
  Multiplexer #(.width(32)) multiplexer_4 (
    .in0(alu_1_res), .in1(DataFromBus), .out(multiplexer_4_out), .sel(control_1_aluvsmemselect));
  Bit_Extender #(.in_width(32), .out_width(26)) bit_extender_3 (.in(rom_1_data), .out(bit_extender_3_out));
  // Probe on control_1_rs
  // Probe on control_1_rd
  // Probe on rom_1_data
  // Probe on control_1_rt
  Multiplexer #(.width(32)) multiplexer_5 (
    .in0(multiplexer_4_out), .in1(adder_1_out), .out(multiplexer_5_out), .sel(or_2_out));
  // Probe on multiplexer_5_out
  Comparator #(.width(4)) comparator_1 (.a(control_1_j_bne_beq), .b(4'b0111), .eq(comparator_1_eq));  // open: gt, lt
  Comparator #(.width(4)) comparator_2 (.a(control_1_j_bne_beq), .b(4'b0001), .eq(comparator_2_eq));  // open: gt, lt
  Comparator #(.width(4)) comparator_3 (.a(control_1_j_bne_beq), .b(4'b0010), .eq(comparator_3_eq));  // open: gt, lt
  Comparator #(.width(4)) comparator_4 (.a(control_1_j_bne_beq), .b(4'b0011), .eq(comparator_4_eq));  // open: gt, lt
  Comparator #(.width(4)) comparator_5 (.a(control_1_j_bne_beq), .b(4'b0100));  // open: gt, eq, lt
  regfile regfile_1 (
    .rd_data(multiplexer_5_out), .write_e(control_1_reg_write_e), .rs(control_1_rs), .rd(control_1_rd),
    .rt(control_1_rt), .rs_data(regfile_1_rs_data), .rt_data(DataToBus));
  Comparator #(.width(4)) comparator_6 (.a(4'b0110), .b(control_1_j_bne_beq), .eq(comparator_6_eq));  // open: gt, lt
  Comparator #(.width(4)) comparator_7 (.a(4'b0101), .b(control_1_j_bne_beq), .eq(comparator_7_eq));  // open: gt, lt
  Control control_1 (
    .Inst(rom_1_data), .ALU_code(control_1_alu_code), .reg_write_e(control_1_reg_write_e),
    .imm_sel(control_1_imm_sel), .ALUvsMemSelect(control_1_aluvsmemselect), .WE_Memory(BusWriteEnable),
    .imm(control_1_imm), .rs(control_1_rs), .rd(control_1_rd), .rt(control_1_rt),
    .j_bne_beq(control_1_j_bne_beq));
  Multiplexer #(.width(32)) multiplexer_6 (
    .in0(regfile_1_rs_data), .in1(multiplexer_5_out), .out(multiplexer_6_out), .sel(or_2_out));
  or or_2 (or_2_out, comparator_2_eq, comparator_4_eq);
  or or_3 (or_3_out, comparator_3_eq, comparator_4_eq);
  and and_1 (and_1_out, comparator_6_eq, not_1_out);
  and and_2 (and_2_out, comparator_7_eq, alu_1_equal);
  Multiplexer #(.width(32)) multiplexer_7 (
    .in0(multiplexer_6_out), .in1(DataToBus), .out(multiplexer_7_out), .sel(or_5_out));
  Multiplexer #(.width(32)) multiplexer_8 (
    .in0(DataToBus), .in1(control_1_imm), .out(multiplexer_8_out), .sel(control_1_imm_sel));
  or or_4 (or_4_out, comparator_1_eq, comparator_2_eq, comparator_3_eq, comparator_4_eq);
  // Probe on control_1_imm_sel
  // Probe on control_1_reg_write_e
  // Probe on control_1_alu_code
  // Probe on multiplexer_7_out
  // Probe on multiplexer_8_out
  not not_1 (not_1_out, alu_1_equal);
  Comparator #(.width(4)) comparator_8 (.a(control_1_alu_code), .b(4'b0110), .eq(comparator_8_eq));  // open: gt, lt
  Comparator #(.width(4)) comparator_9 (.a(control_1_alu_code), .b(4'b0111), .eq(comparator_9_eq));  // open: gt, lt
  // Probe on alu_1_res
  or or_5 (or_5_out, comparator_8_eq, comparator_9_eq);
  Shifter #(.width(32)) shifter_4 (.in(alu_1_res), .\dist (5'b00010), .out(shifter_4_out));
  ALU alu_1 (
    .ALU_CODE(control_1_alu_code), .OP1(multiplexer_7_out), .OP2(multiplexer_8_out), .Res(alu_1_res),
    .Equal(alu_1_equal));
  Bit_Extender #(.in_width(32), .out_width(26)) bit_extender_4 (.in(shifter_4_out), .out(Address));

  // Notes on the sheet:
  //   PC+4
  //   beq/bne
  //   jr/jalr
  //   contents of rom_1 (hex, n*v repeats v):
  //   20100064 2002020 c000007 20500000 1600fffc 2002000a d00c 20080008 41042 3e00008
  //   ALU
  //   PC+4
  //   MEM
  //   j
  //   jal
  //   jr
  //   jalr
  //   syscall
  //   jal/jalr
  //   bne
  //   beq
  //   value from alu
  //   value from mem
  //   sll
  //   srl
endmodule

module regfile (
  input  [31:0] rd_data,
  input  write_e,
  input  [4:0] rs,
  input  [4:0] rd,
  input  [4:0] rt,
  output [31:0] rs_data,
  output [31:0] rt_data
);

  wire clock_1_out, demultiplexer_1_out1, demultiplexer_1_out2, demultiplexer_1_out3, demultiplexer_1_out4,
       demultiplexer_1_out5, demultiplexer_1_out6, demultiplexer_1_out7, demultiplexer_1_out8,
       demultiplexer_1_out9, demultiplexer_1_out10, demultiplexer_1_out11, demultiplexer_1_out12,
       demultiplexer_1_out13, demultiplexer_1_out14, demultiplexer_1_out15, demultiplexer_1_out16,
       demultiplexer_1_out17, demultiplexer_1_out18, demultiplexer_1_out19, demultiplexer_1_out20,
       demultiplexer_1_out21, demultiplexer_1_out22, demultiplexer_1_out23, demultiplexer_1_out24,
       demultiplexer_1_out25, demultiplexer_1_out26, demultiplexer_1_out27, demultiplexer_1_out28,
       demultiplexer_1_out29, demultiplexer_1_out30, demultiplexer_1_out31;
  wire [31:0] a0_q, a1_q, a2_q, a3_q, at_q, fp_q, gp_q, k0_q, k1_q, ra_q, s0_q, s1_q, s2_q, s3_q, s4_q, s5_q,
       s6_q, s7_q, sp_q, t0_q, t1_q, t2_q, t3_q, t4_q, t5_q, t6_q, t7_q, t8_q, t9_q, v0_q, v1_q, Zero_Reg_q;

  Demultiplexer #(.select(5)) demultiplexer_1 (
    .out1(demultiplexer_1_out1), .out2(demultiplexer_1_out2), .out3(demultiplexer_1_out3),
    .out4(demultiplexer_1_out4), .out5(demultiplexer_1_out5), .out6(demultiplexer_1_out6),
    .out7(demultiplexer_1_out7), .out8(demultiplexer_1_out8), .out9(demultiplexer_1_out9),
    .out10(demultiplexer_1_out10), .out11(demultiplexer_1_out11), .out12(demultiplexer_1_out12),
    .out13(demultiplexer_1_out13), .out14(demultiplexer_1_out14), .out15(demultiplexer_1_out15),
    .out16(demultiplexer_1_out16), .out17(demultiplexer_1_out17), .out18(demultiplexer_1_out18),
    .out19(demultiplexer_1_out19), .out20(demultiplexer_1_out20), .out21(demultiplexer_1_out21),
    .out22(demultiplexer_1_out22), .out23(demultiplexer_1_out23), .out24(demultiplexer_1_out24),
    .out25(demultiplexer_1_out25), .out26(demultiplexer_1_out26), .out27(demultiplexer_1_out27),
    .out28(demultiplexer_1_out28), .out29(demultiplexer_1_out29), .out30(demultiplexer_1_out30),
    .out31(demultiplexer_1_out31), .in(write_e), .sel(rd));  // open: out0
  Clock clock_1 (.out(clock_1_out));
  Register #(.width(32)) Zero_Reg (.D({32{1'b0}}), .en(1'b1), .clk(clock_1_out), .Q(Zero_Reg_q));  // open: clr
  Register #(.width(32)) at (.D(rd_data), .en(demultiplexer_1_out1), .clk(clock_1_out), .Q(at_q));  // open: clr
  Register #(.width(32)) v0 (.D(rd_data), .en(demultiplexer_1_out2), .clk(clock_1_out), .Q(v0_q));  // open: clr
  Register #(.width(32)) v1 (.D(rd_data), .en(demultiplexer_1_out3), .clk(clock_1_out), .Q(v1_q));  // open: clr
  Register #(.width(32)) a0 (.D(rd_data), .en(demultiplexer_1_out4), .clk(clock_1_out), .Q(a0_q));  // open: clr
  Register #(.width(32)) a1 (.D(rd_data), .en(demultiplexer_1_out5), .clk(clock_1_out), .Q(a1_q));  // open: clr
  Register #(.width(32)) a2 (.D(rd_data), .en(demultiplexer_1_out6), .clk(clock_1_out), .Q(a2_q));  // open: clr
  Register #(.width(32)) a3 (.D(rd_data), .en(demultiplexer_1_out7), .clk(clock_1_out), .Q(a3_q));  // open: clr
  Register #(.width(32)) t0 (.D(rd_data), .en(demultiplexer_1_out8), .clk(clock_1_out), .Q(t0_q));  // open: clr
  Register #(.width(32)) t1 (.D(rd_data), .en(demultiplexer_1_out9), .clk(clock_1_out), .Q(t1_q));  // open: clr
  Register #(.width(32)) t2 (.D(rd_data), .en(demultiplexer_1_out10), .clk(clock_1_out), .Q(t2_q));  // open: clr
  Register #(.width(32)) t3 (.D(rd_data), .en(demultiplexer_1_out11), .clk(clock_1_out), .Q(t3_q));  // open: clr
  Register #(.width(32)) t4 (.D(rd_data), .en(demultiplexer_1_out12), .clk(clock_1_out), .Q(t4_q));  // open: clr
  Register #(.width(32)) t5 (.D(rd_data), .en(demultiplexer_1_out13), .clk(clock_1_out), .Q(t5_q));  // open: clr
  Register #(.width(32)) t6 (.D(rd_data), .en(demultiplexer_1_out14), .clk(clock_1_out), .Q(t6_q));  // open: clr
  Register #(.width(32)) t7 (.D(rd_data), .en(demultiplexer_1_out15), .clk(clock_1_out), .Q(t7_q));  // open: clr
  Register #(.width(32)) s0 (.D(rd_data), .en(demultiplexer_1_out16), .clk(clock_1_out), .Q(s0_q));  // open: clr
  Register #(.width(32)) s1 (.D(rd_data), .en(demultiplexer_1_out17), .clk(clock_1_out), .Q(s1_q));  // open: clr
  Register #(.width(32)) s2 (.D(rd_data), .en(demultiplexer_1_out18), .clk(clock_1_out), .Q(s2_q));  // open: clr
  Register #(.width(32)) s3 (.D(rd_data), .en(demultiplexer_1_out19), .clk(clock_1_out), .Q(s3_q));  // open: clr
  Register #(.width(32)) s4 (.D(rd_data), .en(demultiplexer_1_out20), .clk(clock_1_out), .Q(s4_q));  // open: clr
  Register #(.width(32)) s5 (.D(rd_data), .en(demultiplexer_1_out21), .clk(clock_1_out), .Q(s5_q));  // open: clr
  Register #(.width(32)) s6 (.D(rd_data), .en(demultiplexer_1_out22), .clk(clock_1_out), .Q(s6_q));  // open: clr
  Register #(.width(32)) s7 (.D(rd_data), .en(demultiplexer_1_out23), .clk(clock_1_out), .Q(s7_q));  // open: clr
  Register #(.width(32)) t8 (.D(rd_data), .en(demultiplexer_1_out24), .clk(clock_1_out), .Q(t8_q));  // open: clr
  Register #(.width(32)) t9 (.D(rd_data), .en(demultiplexer_1_out25), .clk(clock_1_out), .Q(t9_q));  // open: clr
  Register #(.width(32)) k0 (.D(rd_data), .en(demultiplexer_1_out26), .clk(clock_1_out), .Q(k0_q));  // open: clr
  Register #(.width(32)) k1 (.D(rd_data), .en(demultiplexer_1_out27), .clk(clock_1_out), .Q(k1_q));  // open: clr
  Register #(.width(32)) gp (.D(rd_data), .en(demultiplexer_1_out28), .clk(clock_1_out), .Q(gp_q));  // open: clr
  Register #(.width(32)) sp (.D(rd_data), .en(demultiplexer_1_out29), .clk(clock_1_out), .Q(sp_q));  // open: clr
  Register #(.width(32)) fp (.D(rd_data), .en(demultiplexer_1_out30), .clk(clock_1_out), .Q(fp_q));  // open: clr
  Register #(.width(32)) ra (.D(rd_data), .en(demultiplexer_1_out31), .clk(clock_1_out), .Q(ra_q));  // open: clr
  Multiplexer #(.select(5), .width(32)) multiplexer_1 (
    .in0(Zero_Reg_q), .in1(at_q), .in2(v0_q), .in3(v1_q), .in4(a0_q), .in5(a1_q), .in6(a2_q), .in7(a3_q),
    .in8(t0_q), .in9(t1_q), .in10(t2_q), .in11(t3_q), .in12(t4_q), .in13(t5_q), .in14(t6_q), .in15(t7_q),
    .in16(s0_q), .in17(s1_q), .in18(s2_q), .in19(s3_q), .in20(s4_q), .in21(s5_q), .in22(s6_q), .in23(s7_q),
    .in24(t8_q), .in25(t9_q), .in26(k0_q), .in27(k1_q), .in28(gp_q), .in29(sp_q), .in30(fp_q), .in31(ra_q),
    .out(rs_data), .sel(rs));
  Multiplexer #(.select(5), .width(32)) multiplexer_2 (
    .in0(Zero_Reg_q), .in1(at_q), .in2(v0_q), .in3(v1_q), .in4(a0_q), .in5(a1_q), .in6(a2_q), .in7(a3_q),
    .in8(t0_q), .in9(t1_q), .in10(t2_q), .in11(t3_q), .in12(t4_q), .in13(t5_q), .in14(t6_q), .in15(t7_q),
    .in16(s0_q), .in17(s1_q), .in18(s2_q), .in19(s3_q), .in20(s4_q), .in21(s5_q), .in22(s6_q), .in23(s7_q),
    .in24(t8_q), .in25(t9_q), .in26(k0_q), .in27(k1_q), .in28(gp_q), .in29(sp_q), .in30(fp_q), .in31(ra_q),
    .out(rt_data), .sel(rt));
endmodule

module ALU (
  input  [3:0] ALU_CODE,
  input  [31:0] OP1,
  input  [31:0] OP2,
  output [31:0] Res,
  output Equal
);

  wire and_1_out, bit_extender_3_out, bit_extender_4_out, bit_extender_5_out, bit_extender_6_out,
       bit_extender_7_out, bit_extender_8_out, bit_extender_9_out, bit_extender_10_out, clock_1_out,
       comparator_1_lt, comparator_2_eq, comparator_3_eq, comparator_4_eq, comparator_5_eq, comparator_6_eq,
       comparator_7_eq, comparator_8_eq, comparator_9_eq, comparator_10_eq, comparator_11_eq,
       comparator_13_eq, comparator_14_eq, nor_1_out, or_1_out, or_2_out, xor_1_out;
  wire [1:0] multiplexer_11_out, multiplexer_11_out_2, multiplexer_13_out, multiplexer_13_out_2,
       multiplexer_16_out, multiplexer_18_out;
  wire [4:0] bit_extender_1_out, bit_extender_2_out;
  wire [7:0] multiplexer_7_out, multiplexer_9_out;
  wire [15:0] multiplexer_1_out, multiplexer_3_out;
  wire [31:0] adder_1_out, adder_2_out, adder_3_out, adder_4_out, adder_5_out, adder_6_out, adder_7_out,
       adder_8_out, adder_9_out, adder_10_out, adder_11_out, bit_extender_11_out, bit_extender_12_out,
       bit_extender_13_out, bit_extender_14_out, bit_extender_15_out, divider_1_out, divider_1_rem, HI_q,
       LO_q, multiplexer_2_out, multiplexer_4_out, multiplexer_5_out, multiplexer_6_out, multiplexer_8_out,
       multiplexer_10_out, multiplexer_12_out, multiplexer_14_out, multiplexer_17_out, multiplexer_19_out,
       multiplexer_21_out, multiplexer_23_out, multiplier_1_cout, multiplier_1_out, shifter_1_out,
       shifter_2_out, shifter_3_out, subtractor_1_out;

  Bit_Extender #(.in_width(32), .out_width(5)) bit_extender_1 (.in(OP2), .out(bit_extender_1_out));
  Bit_Extender #(.in_width(32), .out_width(5)) bit_extender_2 (.in(OP2), .out(bit_extender_2_out));
  Bit_Extender #(.in_width(32), .out_width(1)) bit_extender_3 (.in(OP1), .out(bit_extender_3_out));
  Bit_Extender #(.in_width(32), .out_width(1)) bit_extender_4 (.in(OP2), .out(bit_extender_4_out));
  Bit_Extender #(.in_width(32), .out_width(1)) bit_extender_5 (.in(OP1), .out(bit_extender_5_out));
  Bit_Extender #(.in_width(32), .out_width(1)) bit_extender_6 (.in(OP2), .out(bit_extender_6_out));
  Bit_Extender #(.in_width(32), .out_width(1)) bit_extender_7 (.in(OP1), .out(bit_extender_7_out));
  Bit_Extender #(.in_width(32), .out_width(1)) bit_extender_8 (.in(OP2), .out(bit_extender_8_out));
  Bit_Extender #(.in_width(32), .out_width(1)) bit_extender_9 (.in(OP1), .out(bit_extender_9_out));
  Bit_Extender #(.in_width(32), .out_width(1)) bit_extender_10 (.in(OP2), .out(bit_extender_10_out));
  Adder #(.width(32)) adder_1 (.a(OP1), .b(OP2), .out(adder_1_out));  // open: cin, cout
  Subtractor #(.width(32)) subtractor_1 (.a(OP1), .b(OP2), .out(subtractor_1_out));  // open: bin, bout
  Multiplier #(.width(32)) multiplier_1 (
    .a(OP1), .b(OP2), .out(multiplier_1_out), .cout(multiplier_1_cout));  // open: cin
  Divider #(.width(32)) divider_1 (.a(OP1), .b(OP2), .out(divider_1_out), .rem(divider_1_rem));  // open: upper
  Shifter #(.width(32)) shifter_1 (.in(OP1), .\dist (bit_extender_1_out), .out(shifter_1_out));
  Shifter #(.shift("lr"), .width(32)) shifter_2 (.in(OP1), .\dist (bit_extender_2_out), .out(shifter_2_out));
  Comparator #(.width(32)) comparator_1 (.a(OP1), .b(OP2), .lt(comparator_1_lt));  // open: gt, eq
  and and_1 (and_1_out, bit_extender_3_out, bit_extender_4_out);
  or or_1 (or_1_out, bit_extender_5_out, bit_extender_6_out);
  nor nor_1 (nor_1_out, bit_extender_7_out, bit_extender_8_out);
  xor xor_1 (xor_1_out, bit_extender_9_out, bit_extender_10_out);
  Shifter #(.width(32)) shifter_3 (.in(OP2), .\dist (5'b10000), .out(shifter_3_out));
  Comparator #(.width(16)) comparator_2 (.a(OP1[31:16]), .b(16'h1), .eq(comparator_2_eq));  // open: gt, lt
  Comparator #(.width(16)) comparator_3 (.a(OP1[31:16]), .b({16{1'b0}}), .eq(comparator_3_eq));  // open: gt, lt
  assign bit_extender_11_out = {{31{comparator_1_lt}}, comparator_1_lt};  // Bit_Extender bit_extender_11
  assign bit_extender_12_out = {{31{and_1_out}}, and_1_out};  // Bit_Extender bit_extender_12
  assign bit_extender_13_out = {{31{or_1_out}}, or_1_out};  // Bit_Extender bit_extender_13
  assign bit_extender_14_out = {{31{nor_1_out}}, nor_1_out};  // Bit_Extender bit_extender_14
  assign bit_extender_15_out = {{31{xor_1_out}}, xor_1_out};  // Bit_Extender bit_extender_15
  Multiplexer #(.width(16)) multiplexer_1 (
    .in0(OP1[31:16]), .in1(OP1[15:0]), .out(multiplexer_1_out), .sel(comparator_2_eq));
  Multiplexer #(.width(32)) multiplexer_2 (
    .in0({32{1'b0}}), .in1(32'h10), .out(multiplexer_2_out), .sel(comparator_2_eq));
  Multiplexer #(.width(16)) multiplexer_3 (
    .in0(OP1[31:16]), .in1(OP1[15:0]), .out(multiplexer_3_out), .sel(comparator_3_eq));
  Multiplexer #(.width(32)) multiplexer_4 (
    .in0({32{1'b0}}), .in1(32'h10), .out(multiplexer_4_out), .sel(comparator_3_eq));
  Comparator #(.width(4)) comparator_4 (.a(ALU_CODE), .b(4'b0010), .eq(comparator_4_eq));  // open: gt, lt
  Comparator #(.width(4)) comparator_5 (.a(ALU_CODE), .b(4'b0011), .eq(comparator_5_eq));  // open: gt, lt
  Multiplexer #(.width(32)) multiplexer_5 (
    .in0(multiplier_1_cout), .in1(divider_1_rem), .out(multiplexer_5_out), .sel(comparator_5_eq));
  Multiplexer #(.width(32)) multiplexer_6 (
    .in0(multiplier_1_out), .in1(divider_1_out), .out(multiplexer_6_out), .sel(comparator_5_eq));
  Adder #(.width(32)) adder_2 (.a({32{1'b0}}), .b(multiplexer_2_out), .out(adder_2_out));  // open: cin, cout
  Adder #(.width(32)) adder_3 (.a({32{1'b0}}), .b(multiplexer_4_out), .out(adder_3_out));  // open: cin, cout
  Register #(.width(32)) HI (.D(multiplexer_5_out), .en(or_2_out), .clk(clock_1_out), .Q(HI_q));  // open: clr
  Register #(.width(32)) LO (.D(multiplexer_6_out), .en(or_2_out), .clk(clock_1_out), .Q(LO_q));  // open: clr
  Clock clock_1 (.out(clock_1_out));
  Multiplexer #(.width(8)) multiplexer_7 (
    .in0(multiplexer_1_out[15:8]), .in1(multiplexer_1_out[7:0]), .out(multiplexer_7_out),
    .sel(comparator_6_eq));
  Comparator comparator_6 (.a(multiplexer_1_out[15:8]), .b(8'h1), .eq(comparator_6_eq));  // open: gt, lt
  Multiplexer #(.width(32)) multiplexer_8 (
    .in0({32{1'b0}}), .in1(32'h8), .out(multiplexer_8_out), .sel(comparator_6_eq));
  Multiplexer #(.width(8)) multiplexer_9 (
    .in0(multiplexer_3_out[15:8]), .in1(multiplexer_3_out[7:0]), .out(multiplexer_9_out),
    .sel(comparator_7_eq));
  Comparator comparator_7 (.a(multiplexer_3_out[15:8]), .b({8{1'b0}}), .eq(comparator_7_eq));  // open: gt, lt
  Multiplexer #(.width(32)) multiplexer_10 (
    .in0({32{1'b0}}), .in1(32'h8), .out(multiplexer_10_out), .sel(comparator_7_eq));
  or or_2 (or_2_out, comparator_4_eq, comparator_5_eq);
  Adder #(.width(32)) adder_4 (.a(multiplexer_8_out), .b(adder_2_out), .out(adder_4_out));  // open: cin, cout
  Adder #(.width(32)) adder_5 (.a(multiplexer_10_out), .b(adder_3_out), .out(adder_5_out));  // open: cin, cout
  Comparator #(.width(4)) comparator_8 (.a(multiplexer_7_out[7:4]), .b(4'b0001), .eq(comparator_8_eq));  // open: gt, lt
  Adder #(.width(32)) adder_6 (.a(multiplexer_12_out), .b(adder_4_out), .out(adder_6_out));  // open: cin, cout
  Comparator #(.width(4)) comparator_9 (.a(multiplexer_9_out[7:4]), .b(4'b0000), .eq(comparator_9_eq));  // open: gt, lt
  Adder #(.width(32)) adder_7 (.a(multiplexer_14_out), .b(adder_5_out), .out(adder_7_out));  // open: cin, cout
  Multiplexer #(.width(4)) multiplexer_11 (
    .in0(multiplexer_7_out[7:4]), .in1(multiplexer_7_out[3:0]),
    .out({multiplexer_11_out_2, multiplexer_11_out}), .sel(comparator_8_eq));
  Multiplexer #(.width(32)) multiplexer_12 (
    .in0({32{1'b0}}), .in1(32'h4), .out(multiplexer_12_out), .sel(comparator_8_eq));
  Multiplexer #(.width(4)) multiplexer_13 (
    .in0(multiplexer_9_out[7:4]), .in1(multiplexer_9_out[3:0]),
    .out({multiplexer_13_out_2, multiplexer_13_out}), .sel(comparator_9_eq));
  Multiplexer #(.width(32)) multiplexer_14 (
    .in0({32{1'b0}}), .in1(32'h4), .out(multiplexer_14_out), .sel(comparator_9_eq));
  Multiplexer #(.select(4), .width(32)) multiplexer_15 (
    .in0(adder_1_out), .in1(subtractor_1_out), .in4(LO_q), .in5(HI_q), .in6(shifter_1_out),
    .in7(shifter_2_out), .in8(bit_extender_11_out), .in9(bit_extender_12_out), .in10(bit_extender_13_out),
    .in11(bit_extender_14_out), .in12(bit_extender_15_out), .in13(shifter_3_out), .in14(adder_10_out),
    .in15(adder_11_out), .out(Res), .sel(ALU_CODE));  // open: in2, in3
  Comparator #(.width(2)) comparator_10 (.a(multiplexer_11_out_2), .b(2'b01), .eq(comparator_10_eq));  // open: gt, lt
  Adder #(.width(32)) adder_8 (.a(multiplexer_17_out), .b(adder_6_out), .out(adder_8_out));  // open: cin, cout
  Comparator #(.width(2)) comparator_11 (.a(multiplexer_13_out_2), .b(2'b00), .eq(comparator_11_eq));  // open: gt, lt
  Adder #(.width(32)) adder_9 (.a(multiplexer_19_out), .b(adder_7_out), .out(adder_9_out));  // open: cin, cout
  Multiplexer #(.width(2)) multiplexer_16 (
    .in0(multiplexer_11_out_2), .in1(multiplexer_11_out), .out(multiplexer_16_out), .sel(comparator_10_eq));
  Multiplexer #(.width(32)) multiplexer_17 (
    .in0({32{1'b0}}), .in1(32'h2), .out(multiplexer_17_out), .sel(comparator_10_eq));
  Multiplexer #(.width(2)) multiplexer_18 (
    .in0(multiplexer_13_out_2), .in1(multiplexer_13_out), .out(multiplexer_18_out), .sel(comparator_11_eq));
  Multiplexer #(.width(32)) multiplexer_19 (
    .in0({32{1'b0}}), .in1(32'h2), .out(multiplexer_19_out), .sel(comparator_11_eq));
  Comparator #(.width(32)) comparator_12 (.a(OP1), .b(OP2), .eq(Equal));  // open: gt, lt
  Comparator #(.width(1)) comparator_13 (.a(multiplexer_16_out[1]), .b(1'b1), .eq(comparator_13_eq));  // open: gt, lt
  Adder #(.width(32)) adder_10 (.a(multiplexer_21_out), .b(adder_8_out), .out(adder_10_out));  // open: cin, cout
  Adder #(.width(32)) adder_11 (.a(multiplexer_23_out), .b(adder_9_out), .out(adder_11_out));  // open: cin, cout
  Multiplexer multiplexer_20 (
    .in0(multiplexer_16_out[1]), .in1(multiplexer_16_out[0]), .sel(comparator_13_eq));  // open: out
  Multiplexer #(.width(32)) multiplexer_21 (
    .in0({32{1'b0}}), .in1(32'h1), .out(multiplexer_21_out), .sel(comparator_13_eq));
  Multiplexer multiplexer_22 (
    .in0(multiplexer_18_out[1]), .in1(multiplexer_18_out[0]), .sel(comparator_14_eq));  // open: out
  Comparator #(.width(1)) comparator_14 (.a(multiplexer_18_out[1]), .b(1'b0), .eq(comparator_14_eq));  // open: gt, lt
  Multiplexer #(.width(32)) multiplexer_23 (
    .in0({32{1'b0}}), .in1(32'h1), .out(multiplexer_23_out), .sel(comparator_14_eq));

  // Notes on the sheet:
  //   clo
  //   clz
  //   Add
  //   Sub
  //   sll
  //   srl
  //   slt
  //   lui
  //   Upper
  //   Lower
  //   mult
  //   div
endmodule

module Control (
  input  [31:0] Inst,
  output [3:0] ALU_code,
  output reg_write_e,
  output imm_sel,
  output ALUvsMemSelect,
  output WE_Memory,
  output [31:0] imm,
  output [4:0] rs,
  output [4:0] rd,
  output [4:0] rt,
  output [3:0] j_bne_beq
);

  wire and1_out, clo_out, clz_out, comparator_1_eq, comparator_2_eq, comparator_3_eq, comparator_4_eq,
       comparator_5_eq, comparator_6_eq, comparator_7_eq, comparator_8_eq, comparator_9_eq, comparator_10_eq,
       comparator_11_eq, comparator_12_eq, comparator_13_eq, comparator_14_eq, comparator_15_eq,
       comparator_16_eq, comparator_17_eq, comparator_18_eq, comparator_19_eq, comparator_22_eq,
       comparator_23_eq, comparator_24_eq, comparator_25_eq, comparator_26_eq, comparator_27_eq,
       comparator_28_eq, comparator_29_eq, comparator_30_eq, comparator_31_eq, comparator_32_eq,
       comparator_33_eq, comparator_34_eq, comparator_35_eq, comparator_36_eq, comparator_37_eq,
       comparator_38_eq, comparator_39_eq, comparator_40_eq, comparator_41_eq, comparator_42_eq,
       comparator_43_eq, comparator_44_eq, comparator_45_eq, comparator_46_eq, comparator_47_eq, div_out,
       jalr_out, jr_out, mfhi_out, mflo_out, mult_out, nor1_out, or1_out, or_1_out, or_11_out, sll1_out,
       slt_out, srl1_out, sub_out, xor1_out;
  wire [1:0] shamt_out;
  wire [2:0] or_9_out;
  wire [20:0] bit_extender_1_out, bit_extender_2_out, multiplexer_3_out;

  Comparator #(.mode("unsigned"), .width(6)) comparator_1 (
    .a(Inst[5:0]), .b(6'b100000), .eq(comparator_1_eq));  // open: gt, lt
  Comparator #(.width(6)) comparator_2 (.a(Inst[31:26]), .b({6{1'b0}}), .eq(comparator_2_eq));  // open: gt, lt
  Comparator #(.width(6)) comparator_3 (.a(Inst[31:26]), .b(6'b001000), .eq(comparator_3_eq));  // open: gt, lt
  Comparator #(.mode("unsigned"), .width(6)) comparator_4 (
    .a(Inst[5:0]), .b(6'b100010), .eq(comparator_4_eq));  // open: gt, lt
  Comparator #(.width(6)) comparator_5 (.a(Inst[31:26]), .b({6{1'b0}}), .eq(comparator_5_eq));  // open: gt, lt
  Comparator #(.mode("unsigned"), .width(6)) comparator_6 (
    .a(Inst[5:0]), .b(6'b011000), .eq(comparator_6_eq));  // open: gt, lt
  Comparator #(.width(6)) comparator_7 (.a(Inst[31:26]), .b({6{1'b0}}), .eq(comparator_7_eq));  // open: gt, lt
  Comparator #(.mode("unsigned"), .width(6)) comparator_8 (
    .a(Inst[5:0]), .b(6'b011010), .eq(comparator_8_eq));  // open: gt, lt
  Comparator #(.width(6)) comparator_9 (.a(Inst[31:26]), .b({6{1'b0}}), .eq(comparator_9_eq));  // open: gt, lt
  Comparator #(.mode("unsigned"), .width(6)) comparator_10 (
    .a(Inst[5:0]), .b(6'b010010), .eq(comparator_10_eq));  // open: gt, lt
  Comparator #(.width(6)) comparator_11 (.a(Inst[31:26]), .b({6{1'b0}}), .eq(comparator_11_eq));  // open: gt, lt
  Comparator #(.mode("unsigned"), .width(6)) comparator_12 (
    .a(Inst[5:0]), .b(6'b010000), .eq(comparator_12_eq));  // open: gt, lt
  Comparator #(.width(6)) comparator_13 (.a(Inst[31:26]), .b({6{1'b0}}), .eq(comparator_13_eq));  // open: gt, lt
  Comparator #(.mode("unsigned"), .width(6)) comparator_14 (
    .a(Inst[5:0]), .b(6'b101010), .eq(comparator_14_eq));  // open: gt, lt
  Comparator #(.width(6)) comparator_15 (.a(Inst[31:26]), .b({6{1'b0}}), .eq(comparator_15_eq));  // open: gt, lt
  Comparator #(.mode("unsigned"), .width(6)) comparator_16 (
    .a(Inst[5:0]), .b({6{1'b0}}), .eq(comparator_16_eq));  // open: gt, lt
  Comparator #(.width(6)) comparator_17 (.a(Inst[31:26]), .b({6{1'b0}}), .eq(comparator_17_eq));  // open: gt, lt
  Comparator #(.mode("unsigned"), .width(6)) comparator_18 (
    .a(Inst[5:0]), .b(6'b000010), .eq(comparator_18_eq));  // open: gt, lt
  Comparator #(.width(6)) comparator_19 (.a(Inst[31:26]), .b({6{1'b0}}), .eq(comparator_19_eq));  // open: gt, lt
  Comparator #(.width(6)) comparator_20 (.a(Inst[31:26]), .b(6'b100011), .eq(ALUvsMemSelect));  // open: gt, lt
  Comparator #(.width(6)) comparator_21 (.a(Inst[31:26]), .b(6'b101011), .eq(WE_Memory));  // open: gt, lt
  Comparator #(.width(6)) comparator_22 (.a(Inst[31:26]), .b(6'b000100), .eq(comparator_22_eq));  // open: gt, lt
  Comparator #(.width(6)) comparator_23 (.a(Inst[31:26]), .b(6'b000101), .eq(comparator_23_eq));  // open: gt, lt
  Comparator #(.width(6)) comparator_24 (.a(Inst[5:0]), .b(6'b100100), .eq(comparator_24_eq));  // open: gt, lt
  Comparator #(.width(6)) comparator_25 (.a(Inst[31:26]), .b({6{1'b0}}), .eq(comparator_25_eq));  // open: gt, lt
  Comparator #(.width(6)) comparator_26 (.a(Inst[5:0]), .b(6'b100101), .eq(comparator_26_eq));  // open: gt, lt
  Comparator #(.width(6)) comparator_27 (.a(Inst[31:26]), .b(6'b001000), .eq(comparator_27_eq));  // open: gt, lt
  Comparator #(.width(6)) comparator_28 (.a(Inst[5:0]), .b(6'b100111), .eq(comparator_28_eq));  // open: gt, lt
  Comparator #(.width(6)) comparator_29 (.a(Inst[31:26]), .b({6{1'b0}}), .eq(comparator_29_eq));  // open: gt, lt
  Comparator #(.width(6)) comparator_30 (.a(Inst[5:0]), .b(6'b100110), .eq(comparator_30_eq));  // open: gt, lt
  Comparator #(.width(6)) comparator_31 (.a(Inst[31:26]), .b({6{1'b0}}), .eq(comparator_31_eq));  // open: gt, lt
  Comparator #(.width(6)) comparator_32 (.a(Inst[31:26]), .b(6'b001100), .eq(comparator_32_eq));  // open: gt, lt
  Comparator #(.width(6)) comparator_33 (.a(Inst[31:26]), .b(6'b001101), .eq(comparator_33_eq));  // open: gt, lt
  Comparator #(.width(6)) comparator_34 (.a(Inst[31:26]), .b(6'b001110), .eq(comparator_34_eq));  // open: gt, lt
  Comparator #(.width(6)) comparator_35 (.a(Inst[31:26]), .b(6'b001111), .eq(comparator_35_eq));  // open: gt, lt
  Comparator #(.width(6)) comparator_36 (.a(Inst[5:0]), .b(6'b100001), .eq(comparator_36_eq));  // open: gt, lt
  Comparator #(.width(6)) comparator_37 (.a(Inst[31:26]), .b(6'b011100), .eq(comparator_37_eq));  // open: gt, lt
  Comparator #(.width(6)) comparator_38 (.a(Inst[5:0]), .b(6'b100000), .eq(comparator_38_eq));  // open: gt, lt
  Comparator #(.width(6)) comparator_39 (.a(Inst[31:26]), .b(6'b011100), .eq(comparator_39_eq));  // open: gt, lt
  Comparator #(.width(6)) comparator_40 (.a(Inst[31:26]), .b(6'b000010), .eq(comparator_40_eq));  // open: gt, lt
  Comparator #(.width(6)) comparator_41 (.a(Inst[31:26]), .b(6'b000011), .eq(comparator_41_eq));  // open: gt, lt
  Comparator #(.width(6)) comparator_42 (.a(Inst[5:0]), .b(6'b001000), .eq(comparator_42_eq));  // open: gt, lt
  Comparator #(.width(6)) comparator_43 (.a(Inst[31:26]), .b({6{1'b0}}), .eq(comparator_43_eq));  // open: gt, lt
  Comparator #(.width(6)) comparator_44 (.a(Inst[5:0]), .b(6'b001001), .eq(comparator_44_eq));  // open: gt, lt
  Comparator #(.width(6)) comparator_45 (.a(Inst[31:26]), .b({6{1'b0}}), .eq(comparator_45_eq));  // open: gt, lt
  Comparator #(.width(6)) comparator_46 (.a(Inst[5:0]), .b(6'b001100), .eq(comparator_46_eq));  // open: gt, lt
  Comparator #(.width(6)) comparator_47 (.a(Inst[31:26]), .b({6{1'b0}}), .eq(comparator_47_eq));  // open: gt, lt
  // AND_Gate add has open pins: in0=comparator_1_eq, in1=comparator_2_eq, out=open
  and sub (sub_out, comparator_4_eq, comparator_5_eq);
  and mult (mult_out, comparator_6_eq, comparator_7_eq);
  and div (div_out, comparator_8_eq, comparator_9_eq);
  and mflo (mflo_out, comparator_10_eq, comparator_11_eq);
  and mfhi (mfhi_out, comparator_12_eq, comparator_13_eq);
  and slt (slt_out, comparator_14_eq, comparator_15_eq);
  and sll1 (sll1_out, comparator_16_eq, comparator_17_eq);
  and srl1 (srl1_out, comparator_18_eq, comparator_19_eq);
  and and1 (and1_out, comparator_24_eq, comparator_25_eq);
  and or1 (or1_out, comparator_26_eq, comparator_27_eq);
  and nor1 (nor1_out, comparator_28_eq, comparator_29_eq);
  and xor1 (xor1_out, comparator_30_eq, comparator_31_eq);
  and clo (clo_out, comparator_36_eq, comparator_37_eq);
  and clz (clz_out, comparator_38_eq, comparator_39_eq);
  and jr (jr_out, comparator_42_eq, comparator_43_eq);
  and jalr (jalr_out, comparator_44_eq, comparator_45_eq);
  and syscall (or_9_out[2], comparator_46_eq, comparator_47_eq);
  or or_1 (or_1_out, clo_out, clz_out, jr_out, jalr_out, or_9_out[2]);
  or or_2 (ALU_code[0], comparator_22_eq, sub_out, div_out, mfhi_out, srl1_out, and1_out, nor1_out, comparator_32_eq, comparator_35_eq, clz_out, comparator_23_eq);
  Multiplexer #(.width(5)) multiplexer_1 (.in0(Inst[20:16]), .in1({5{1'b0}}), .out(rt), .sel(or_1_out));
  or or_3 (ALU_code[1], mult_out, div_out, sll1_out, srl1_out, or1_out, nor1_out, comparator_33_eq, clo_out, clz_out);
  or or_4 (j_bne_beq[1], comparator_23_eq, jr_out, jalr_out);
  or or_5 (ALU_code[2], mflo_out, mfhi_out, sll1_out, srl1_out, xor1_out, comparator_34_eq, comparator_35_eq, clo_out, clz_out);
  or or_6 (j_bne_beq[0], comparator_22_eq, comparator_41_eq, jalr_out);
  or or_7 (j_bne_beq[2], comparator_22_eq, comparator_23_eq, or_9_out[2]);
  or or_8 (ALU_code[3], slt_out, and1_out, or1_out, nor1_out, xor1_out, comparator_32_eq, comparator_33_eq, comparator_34_eq, comparator_35_eq, clo_out, clz_out);
  or or_9 (or_9_out[0], mult_out, div_out, comparator_41_eq, jalr_out);
  or or_10 (or_9_out[1], comparator_3_eq, ALUvsMemSelect, WE_Memory, comparator_22_eq, comparator_23_eq, comparator_32_eq, comparator_33_eq, comparator_34_eq, comparator_35_eq, comparator_41_eq);
  Multiplexer multiplexer_2 (.in0(1'b1), .in1(1'b0), .out(reg_write_e), .sel(or_11_out));
  or or_11 (or_11_out, mult_out, div_out, WE_Memory, comparator_22_eq, comparator_23_eq, comparator_41_eq, jr_out, or_9_out[2]);
  or or_12 (imm_sel, comparator_3_eq, ALUvsMemSelect, WE_Memory, sll1_out, srl1_out, comparator_32_eq, comparator_33_eq, comparator_34_eq, clo_out);
  assign bit_extender_1_out = {{5{Inst[15]}}, Inst[15:0]};  // Bit_Extender bit_extender_1
  assign bit_extender_2_out = {{16{Inst[10]}}, Inst[10:6]};  // Bit_Extender bit_extender_2
  // Probe on reg_write_e
  // Probe on or_11_out
  or shamt (shamt_out[0], sll1_out, srl1_out);
  Multiplexer #(.select(2), .width(21)) multiplexer_3 (
    .in0(bit_extender_1_out), .in1(bit_extender_2_out), .in2(Inst[20:0]), .out(multiplexer_3_out),
    .sel(shamt_out));  // open: in3
  or or_13 (shamt_out[1], comparator_41_eq, comparator_40_eq);
  Multiplexer #(.select(3), .width(5)) multiplexer_4 (
    .in0(Inst[15:11]), .in1({5{1'b0}}), .in2(Inst[20:16]), .in3({5{1'b1}}), .in4(5'b01010), .out(rd),
    .sel(or_9_out));  // open: in5, in6, in7
  assign imm = {{11{multiplexer_3_out[20]}}, multiplexer_3_out};  // Bit_Extender bit_extender_3

  assign j_bne_beq[3] = 1'b0;
  assign rs = Inst[25:21];

  // Notes on the sheet:
  //   Inst: initial=0x12a4020
  //   Func code
  //   Op code
  //   5:0
  //   25:21
  //   Func and Op codes in Hex
  //   15:11
  //   20:16
  //   addi
  //   lw
  //   beq
  //   bne
  //   andi
  //   ori
  //   xori
  //   lui
  //   10:6
  //   j
  //   jal
  //   sw
endmodule

module KeyboardController (
  input  [31:0] DataFromBus,
  input  WriteEnableFromBus,
  input  [25:0] AddressFromBus,
  input  [6:0] KeyboardData,
  input  KeyboardStatus,
  output KeyboardRead,
  output WriteToBus,
  output [31:0] DataToBus
);

  wire and_2_out, comparator_1_eq, comparator_2_eq, comparator_3_eq, comparator_4_eq, controlled_buffer_1_out;
  wire [6:0] controlled_buffer_2_out;

  and and_1 (KeyboardRead, comparator_1_eq, comparator_2_eq);
  Comparator #(.width(1)) comparator_1 (.a(1'b1), .b(WriteEnableFromBus), .eq(comparator_1_eq));  // open: gt, lt
  Comparator #(.width(26)) comparator_2 (.a(AddressFromBus), .b(26'h3ffff10), .eq(comparator_2_eq));  // open: gt, lt
  Comparator #(.width(1)) comparator_3 (.a(WriteEnableFromBus), .b(1'b0), .eq(comparator_3_eq));  // open: gt, lt
  Comparator #(.width(26)) comparator_4 (.a(AddressFromBus), .b(26'h3ffff14), .eq(comparator_4_eq));  // open: gt, lt
  and and_2 (and_2_out, comparator_3_eq, comparator_2_eq);
  assign DataToBus = {{31{controlled_buffer_1_out}}, controlled_buffer_1_out};  // Bit_Extender bit_extender_1
  assign controlled_buffer_1_out = and_2_out ? KeyboardStatus : 1'bz;  // Controlled_Buffer controlled_buffer_1
  assign controlled_buffer_2_out = comparator_4_eq ? KeyboardData : 7'bz;  // Controlled_Buffer controlled_buffer_2
  assign DataToBus = {{25{controlled_buffer_2_out[6]}}, controlled_buffer_2_out};  // Bit_Extender bit_extender_2

  assign WriteToBus = 1'b0;

  // Notes on the sheet:
  //   delete this constant 0
endmodule

module BuzzerController (
  input  [31:0] DataFromBus,
  input  WE_FromBus,
  input  [25:0] AddressFromBus,
  output [13:0] Frequency,
  output [6:0] Volume,
  output EnableSound
);

  wire and_1_out, and_2_out, and_3_out, clock_1_out, comparator_1_eq, comparator_2_eq, comparator_3_eq,
       not_1_out;
  wire [6:0] bit_extender_1_out;
  wire [13:0] bit_extender_2_out;

  Comparator #(.width(26)) comparator_1 (.a(AddressFromBus), .b(26'h3ffff80), .eq(comparator_1_eq));  // open: gt, lt
  Comparator #(.width(26)) comparator_2 (.a(AddressFromBus), .b(26'h3ffff84), .eq(comparator_2_eq));  // open: gt, lt
  Comparator #(.width(26)) comparator_3 (.a(AddressFromBus), .b(26'h3ffff88), .eq(comparator_3_eq));  // open: gt, lt
  and and_1 (and_1_out, WE_FromBus, comparator_1_eq);
  and and_2 (and_2_out, WE_FromBus, comparator_3_eq);
  Bit_Extender #(.in_width(32), .out_width(7)) bit_extender_1 (.in(DataFromBus), .out(bit_extender_1_out));
  and and_3 (and_3_out, WE_FromBus, comparator_2_eq);
  Bit_Extender #(.in_width(32), .out_width(14)) bit_extender_2 (.in(DataFromBus), .out(bit_extender_2_out));
  not not_1 (not_1_out, EnableSound);
  Clock clock_1 (.out(clock_1_out));
  Register #(.width(14)) register_1 (
    .D(bit_extender_2_out), .en(and_1_out), .clk(clock_1_out), .Q(Frequency));  // open: clr
  Register #(.width(1)) register_2 (.D(not_1_out), .en(and_2_out), .clk(clock_1_out), .Q(EnableSound));  // open: clr
  Register #(.width(7)) register_3 (
    .D(bit_extender_1_out), .en(and_3_out), .clk(clock_1_out), .Q(Volume));  // open: clr
endmodule

module RGBController (
  input  [25:0] AddressFromBus,
  input  [31:0] DataFromBus,
  input  WriteEnable,
  output [7:0] RGBX,
  output [7:0] RGBY,
  output [23:0] RGBColor,
  output RGBWrite
);

  wire and_1_out, clock_1_out, comparator_1_eq, comparator_2_eq, comparator_3_eq;
  wire [7:0] bit_extender_1_out;
  wire [23:0] bit_extender_2_out;

  Comparator #(.width(26)) comparator_1 (.a(AddressFromBus), .b(26'h3ffff20), .eq(comparator_1_eq));  // open: gt, lt
  Comparator #(.width(26)) comparator_2 (.a(AddressFromBus), .b(26'h3ffff24), .eq(comparator_2_eq));  // open: gt, lt
  Comparator #(.width(26)) comparator_3 (.a(AddressFromBus), .b(26'h3ffff28), .eq(comparator_3_eq));  // open: gt, lt
  Comparator #(.width(26)) comparator_4 (.a(AddressFromBus), .b(26'h3ffff2c), .eq(RGBWrite));  // open: gt, lt
  Bit_Extender #(.in_width(32), .out_width(8)) bit_extender_1 (.in(DataFromBus), .out(bit_extender_1_out));
  and and_1 (and_1_out, comparator_1_eq, WriteEnable);
  Bit_Extender #(.in_width(32), .out_width(24)) bit_extender_2 (.in(DataFromBus), .out(bit_extender_2_out));
  Register register_1 (.D(bit_extender_1_out), .en(and_1_out), .clk(clock_1_out), .Q(RGBX));  // open: clr
  Register register_2 (.D(bit_extender_1_out), .en(comparator_2_eq), .clk(clock_1_out), .Q(RGBY));  // open: clr
  Register #(.width(24)) register_3 (
    .D(bit_extender_2_out), .en(comparator_3_eq), .clk(clock_1_out), .Q(RGBColor));  // open: clr
  Clock clock_1 (.out(clock_1_out));
endmodule

module TerminalController (
  input  [25:0] AddressFromBus,
  input  WriteEnableFromBus,
  input  [31:0] DataFromBus,
  output WriteToTerminal,
  output [6:0] DataToTerminal
);

  wire comparator_1_eq, comparator_2_eq;
  wire [6:0] bit_extender_1_out;

  Comparator #(.width(26)) comparator_1 (.a(AddressFromBus), .b(26'h3ffff00), .eq(comparator_1_eq));  // open: gt, lt
  Comparator #(.width(1)) comparator_2 (.a(WriteEnableFromBus), .b(1'b1), .eq(comparator_2_eq));  // open: gt, lt
  Bit_Extender #(.in_width(32), .out_width(7)) bit_extender_1 (.in(DataFromBus), .out(bit_extender_1_out));
  and and_1 (WriteToTerminal, comparator_1_eq, comparator_2_eq);
  Multiplexer #(.width(7)) multiplexer_1 (
    .in1(bit_extender_1_out), .out(DataToTerminal), .sel(WriteToTerminal));  // open: in0
endmodule

module MemoryController (
  input  [25:0] AddressFromBus,
  input  WE_FB,
  input  [31:0] DataFromMem,
  input  [31:0] DataFromBus,
  output [23:0] AddressToMem,
  output WE_TM,
  output WriteToBus,
  output [31:0] DataToBus,
  output [31:0] DataToMem
);

  wire comparator_1_lt, not_1_out;

  Comparator #(.width(26)) comparator_1 (.a(AddressFromBus), .b(26'h3ffff00), .lt(comparator_1_lt));  // open: gt, eq
  not not_1 (not_1_out, WE_FB);
  Bit_Extender #(.in_width(26), .out_width(24)) bit_extender_1 (.in(AddressFromBus), .out(AddressToMem));
  and and_1 (WE_TM, comparator_1_lt, WE_FB);
  and and_2 (WriteToBus, comparator_1_lt, not_1_out);

  assign DataToBus = DataFromMem;
  assign DataToMem = DataFromBus;
endmodule

module Computer (
);

  wire buzzercontroller_1_enablesound, clock_1_out, clock_2_out, clock_4_out, cpumain_1_buswriteenable,
       keyboard_1_avail, keyboardcontroller_1_p6, keyboardcontroller_1_p8, memorycontroller_1_we_tm,
       memorycontroller_1_writetobus, rgb_video_1_p1, rgb_video_1_p2, terminalcontroller_1_writetoterminal;
  wire [6:0] buzzercontroller_1_volume, keyboard_1_data, terminalcontroller_1_datatoterminal;
  wire [7:0] rgb_video_1_p3, rgb_video_1_p4;
  wire [13:0] buzzercontroller_1_frequency;
  wire [23:0] memorycontroller_1_addresstomem, rgb_video_1_p5;
  wire [25:0] cpumain_1_address;
  wire [31:0] cpumain_1_datafrombus, cpumain_1_datatobus, keyboardcontroller_1_p7,
       memorycontroller_1_datatobus, memorycontroller_1_datatomem, ram_1_dout;

  Clock clock_1 (.out(clock_1_out));
  RAM #(.addrWidth(24), .dataWidth(32), .enables("line")) ram_1 (
    .addr(memorycontroller_1_addresstomem), .we(memorycontroller_1_we_tm), .clk(clock_1_out),
    .din(memorycontroller_1_datatomem), .dout(ram_1_dout));
  Clock clock_2 (.out(clock_2_out));
  Keyboard keyboard_1 (
    .clk(clock_2_out), .re(keyboardcontroller_1_p8), .avail(keyboard_1_avail), .data(keyboard_1_data));  // open: clr
  MemoryController memorycontroller_1 (
    .AddressFromBus(cpumain_1_address), .WE_FB(cpumain_1_buswriteenable), .DataFromMem(ram_1_dout),
    .DataFromBus(cpumain_1_datafrombus), .AddressToMem(memorycontroller_1_addresstomem),
    .WE_TM(memorycontroller_1_we_tm), .WriteToBus(memorycontroller_1_writetobus),
    .DataToBus(memorycontroller_1_datatobus), .DataToMem(memorycontroller_1_datatomem));
  CPUmain cpumain_1 (
    .Address(cpumain_1_address), .BusWriteEnable(cpumain_1_buswriteenable), .DataToBus(cpumain_1_datatobus),
    .DataFromBus(cpumain_1_datafrombus));
  // KeyboardController keyboardcontroller_1: pin names not known; wires that end beside it: cpumain_1_datafrombus, cpumain_1_buswriteenable, cpumain_1_address, keyboard_1_data, keyboard_1_avail, keyboardcontroller_1_p6, keyboardcontroller_1_p7, keyboardcontroller_1_p8
  assign cpumain_1_datafrombus = memorycontroller_1_writetobus ? memorycontroller_1_datatobus : 32'bz;  // Controlled_Buffer controlled_buffer_1
  assign cpumain_1_datafrombus = cpumain_1_buswriteenable ? cpumain_1_datatobus : 32'bz;  // Controlled_Buffer controlled_buffer_2
  assign cpumain_1_datafrombus = keyboardcontroller_1_p6 ? keyboardcontroller_1_p7 : 32'bz;  // Controlled_Buffer controlled_buffer_3
  // RGB_Video #(.height(256), .width(256)) rgb_video_1: pin names not known; wires that end beside it: rgb_video_1_p1, rgb_video_1_p2, rgb_video_1_p3, rgb_video_1_p4, rgb_video_1_p5
  Clock clock_3 (.out(rgb_video_1_p1));
  TerminalController terminalcontroller_1 (
    .AddressFromBus(cpumain_1_address), .WriteEnableFromBus(cpumain_1_buswriteenable),
    .DataFromBus(cpumain_1_datafrombus), .WriteToTerminal(terminalcontroller_1_writetoterminal),
    .DataToTerminal(terminalcontroller_1_datatoterminal));
  RGBController rgbcontroller_1 (
    .AddressFromBus(cpumain_1_address), .DataFromBus(cpumain_1_datafrombus),
    .WriteEnable(cpumain_1_buswriteenable), .RGBX(rgb_video_1_p3), .RGBY(rgb_video_1_p4),
    .RGBColor(rgb_video_1_p5), .RGBWrite(rgb_video_1_p2));
  BuzzerController buzzercontroller_1 (
    .DataFromBus(cpumain_1_datafrombus), .WE_FromBus(cpumain_1_buswriteenable),
    .AddressFromBus(cpumain_1_address), .Frequency(buzzercontroller_1_frequency),
    .Volume(buzzercontroller_1_volume), .EnableSound(buzzercontroller_1_enablesound));
  Clock clock_4 (.out(clock_4_out));
  TTY tty_1 (
    .data(terminalcontroller_1_datatoterminal), .clk(clock_4_out), .we(terminalcontroller_1_writetoterminal));  // open: clr
  // Buzzer buzzer_1: pin names not known; wires that end beside it: buzzercontroller_1_frequency, buzzercontroller_1_volume, buzzercontroller_1_enablesound

  // Notes on the sheet:
  //   Data
  //   WE
  //   Address
endmodule
